// Digital circuit 2^N-16.dig as structural Verilog
module _2_N_16 (
  input  [15:0] A,
  output Y
);

  wire and_1_out, and_2_out, and_3_out, and_4_out, and_5_out, and_6_out, and_7_out, and_8_out, not_1_out,
       not_2_out, not_3_out, not_4_out, not_5_out, not_6_out, not_7_out, not_8_out, not_9_out, not_10_out,
       not_11_out, not_12_out, not_13_out, not_14_out, not_15_out, not_16_out, xor_1_out, xor_2_out,
       xor_3_out, xor_4_out, xor_5_out, xor_6_out, xor_7_out, xor_8_out;

  not not_1 (not_1_out, A[0]);
  not not_2 (not_2_out, A[1]);
  not not_3 (not_3_out, A[2]);
  not not_4 (not_4_out, A[3]);
  not not_5 (not_5_out, A[4]);
  not not_6 (not_6_out, A[5]);
  not not_7 (not_7_out, A[6]);
  not not_8 (not_8_out, A[7]);
  not not_9 (not_9_out, A[8]);
  not not_10 (not_10_out, A[9]);
  not not_11 (not_11_out, A[10]);
  not not_12 (not_12_out, A[11]);
  not not_13 (not_13_out, A[12]);
  not not_14 (not_14_out, A[13]);
  not not_15 (not_15_out, A[14]);
  not not_16 (not_16_out, A[15]);
  xor xor_1 (xor_1_out, A[0], A[1]);
  xor xor_2 (xor_2_out, A[2], A[3]);
  xor xor_3 (xor_3_out, A[4], A[5]);
  xor xor_4 (xor_4_out, A[6], A[7]);
  xor xor_5 (xor_5_out, A[8], A[9]);
  xor xor_6 (xor_6_out, A[10], A[11]);
  xor xor_7 (xor_7_out, A[12], A[13]);
  xor xor_8 (xor_8_out, A[14], A[15]);
  and and_1 (and_1_out, xor_1_out, not_3_out, not_4_out, not_5_out, not_6_out, not_7_out, not_8_out, not_9_out, not_10_out, not_11_out, not_12_out, not_13_out, not_14_out, not_15_out, not_16_out);
  and and_2 (and_2_out, not_1_out, not_2_out, xor_2_out, not_5_out, not_6_out, not_7_out, not_8_out, not_9_out, not_10_out, not_11_out, not_12_out, not_13_out, not_14_out, not_15_out, not_16_out);
  and and_3 (and_3_out, not_1_out, not_2_out, not_3_out, not_4_out, xor_3_out, not_7_out, not_8_out, not_9_out, not_10_out, not_11_out, not_12_out, not_13_out, not_14_out, not_15_out, not_16_out);
  and and_4 (and_4_out, not_1_out, not_2_out, not_3_out, not_4_out, not_5_out, not_6_out, xor_4_out, not_9_out, not_10_out, not_11_out, not_12_out, not_13_out, not_14_out, not_15_out, not_16_out);
  and and_5 (and_5_out, not_1_out, not_2_out, not_3_out, not_4_out, not_5_out, not_6_out, not_7_out, not_8_out, xor_5_out, not_11_out, not_12_out, not_13_out, not_14_out, not_15_out, not_16_out);
  and and_6 (and_6_out, not_1_out, not_2_out, not_3_out, not_4_out, not_5_out, not_6_out, not_7_out, not_8_out, not_9_out, not_10_out, xor_6_out, not_13_out, not_14_out, not_15_out, not_16_out);
  and and_7 (and_7_out, not_1_out, not_2_out, not_3_out, not_4_out, not_5_out, not_6_out, not_7_out, not_8_out, not_9_out, not_10_out, not_11_out, not_12_out, xor_7_out, not_15_out, not_16_out);
  and and_8 (and_8_out, not_1_out, not_2_out, not_3_out, not_4_out, not_5_out, not_6_out, not_7_out, not_8_out, not_9_out, not_10_out, not_11_out, not_12_out, not_13_out, not_14_out, xor_8_out);
  or or_1 (Y, and_1_out, and_2_out, and_3_out, and_4_out, and_5_out, and_6_out, and_7_out, and_8_out);
  // Pins of 1 and 16 bits meet at A

  // Notes on the sheet:
  //   detects if the input is 2^n where n is an integer
  //   ie 10000000 or 000010000 or 00000001 etc.
endmodule
