// Digital circuit 2xHA-4.dig as structural Verilog
module _2xHA_4 (
  input  [3:0] A,
  input  [3:0] B,
  output [3:0] SUM,
  output [3:0] CRY
);

  wire fa_1_2_cry, fa_1_3_cry, fa_1_4_cry;

  FA_1 fa_1_1 (.A(A[3]), .B(B[3]), .Cin(fa_1_2_cry), .SUM(SUM[3]), .CRY(CRY[0]));
  FA_1 fa_1_2 (.A(A[2]), .B(B[2]), .Cin(fa_1_3_cry), .SUM(SUM[2]), .CRY(fa_1_2_cry));
  FA_1 fa_1_3 (.A(A[1]), .B(B[1]), .Cin(fa_1_4_cry), .SUM(SUM[1]), .CRY(fa_1_3_cry));
  FA_1 fa_1_4 (.A(A[0]), .B(B[0]), .Cin(1'b0), .SUM(SUM[0]), .CRY(fa_1_4_cry));

  assign CRY[3:1] = 3'b000;
endmodule
