// Digital circuit 2xHA-8.dig as structural Verilog
module _2xHA_8 (
  input  [7:0] A,
  input  [7:0] B,
  output [7:0] SUM,
  output [7:0] CRY
);

  wire fa_1_2_cry, fa_1_3_cry, fa_1_4_cry, fa_1_5_cry, fa_1_6_cry, fa_1_7_cry, fa_1_8_cry;

  FA_1 fa_1_1 (.A(A[7]), .B(B[7]), .Cin(fa_1_2_cry), .SUM(SUM[7]), .CRY(CRY[0]));
  FA_1 fa_1_2 (.A(A[6]), .B(B[6]), .Cin(fa_1_3_cry), .SUM(SUM[6]), .CRY(fa_1_2_cry));
  FA_1 fa_1_3 (.A(A[5]), .B(B[5]), .Cin(fa_1_4_cry), .SUM(SUM[5]), .CRY(fa_1_3_cry));
  FA_1 fa_1_4 (.A(A[4]), .B(B[4]), .Cin(fa_1_5_cry), .SUM(SUM[4]), .CRY(fa_1_4_cry));
  FA_1 fa_1_5 (.A(A[3]), .B(B[3]), .Cin(fa_1_6_cry), .SUM(SUM[3]), .CRY(fa_1_5_cry));
  FA_1 fa_1_6 (.A(A[2]), .B(B[2]), .Cin(fa_1_7_cry), .SUM(SUM[2]), .CRY(fa_1_6_cry));
  FA_1 fa_1_7 (.A(A[1]), .B(B[1]), .Cin(fa_1_8_cry), .SUM(SUM[1]), .CRY(fa_1_7_cry));
  FA_1 fa_1_8 (.A(A[0]), .B(B[0]), .Cin(1'b0), .SUM(SUM[0]), .CRY(fa_1_8_cry));

  assign CRY[7:1] = {7{1'b0}};
endmodule
