// Digital circuit 3xHA-2.dig as structural Verilog
module _3xHA_2 (
  input  [1:0] A,
  input  [1:0] B,
  input  [1:0] C,
  output [1:0] SUM,
  output [1:0] CRY
);

  wire fa_1_2_cry, fa_1_3_cry, fa_1_3_sum, fa_1_4_cry, fa_1_5_cry, fa_1_5_sum;

  FA_1 fa_1_1 (.A(fa_1_2_cry), .B(fa_1_3_cry), .Cin(1'b0), .SUM(CRY[0]), .CRY(CRY[1]));
  FA_1 fa_1_2 (.A(fa_1_3_sum), .B(fa_1_4_cry), .Cin(fa_1_5_cry), .SUM(SUM[1]), .CRY(fa_1_2_cry));
  FA_1 fa_1_3 (.A(A[1]), .B(B[1]), .Cin(C[1]), .SUM(fa_1_3_sum), .CRY(fa_1_3_cry));
  FA_1 fa_1_4 (.A(fa_1_5_sum), .B(C[0]), .Cin(1'b0), .SUM(SUM[0]), .CRY(fa_1_4_cry));
  FA_1 fa_1_5 (.A(A[0]), .B(B[0]), .Cin(1'b0), .SUM(fa_1_5_sum), .CRY(fa_1_5_cry));
endmodule
