// Digital circuit 3xHA-4.dig as structural Verilog
module _3xHA_4 (
  input  [3:0] A,
  input  [3:0] B,
  input  [3:0] C,
  output [3:0] SUM,
  output [3:0] CRY
);

  wire [1:0] _3xha_2_2_cry, _3xha_2_3_cry, _3xha_2_3_sum, _3xha_2_4_cry, _3xha_2_5_cry, _3xha_2_5_sum;

  _3xHA_2 _3xha_2_1 (.A(_3xha_2_2_cry), .B(_3xha_2_3_cry), .C(2'b00), .SUM(CRY[1:0]), .CRY(CRY[3:2]));
  _3xHA_2 _3xha_2_2 (.A(_3xha_2_3_sum), .B(_3xha_2_4_cry), .C(_3xha_2_5_cry), .SUM(SUM[3:2]), .CRY(_3xha_2_2_cry));
  _3xHA_2 _3xha_2_3 (.A(A[3:2]), .B(B[3:2]), .C(C[3:2]), .SUM(_3xha_2_3_sum), .CRY(_3xha_2_3_cry));
  _3xHA_2 _3xha_2_4 (.A(_3xha_2_5_sum), .B(C[1:0]), .C(2'b00), .SUM(SUM[1:0]), .CRY(_3xha_2_4_cry));
  _3xHA_2 _3xha_2_5 (.A(A[1:0]), .B(B[1:0]), .C(2'b00), .SUM(_3xha_2_5_sum), .CRY(_3xha_2_5_cry));
endmodule
