// Digital circuit 3xHA-8.dig as structural Verilog
module _3xHA_8 (
  input  [7:0] A,
  input  [7:0] B,
  input  [7:0] C,
  output [7:0] SUM,
  output [7:0] CRY
);

  wire [3:0] _3xha_4_2_cry, _3xha_4_3_cry, _3xha_4_3_sum, _3xha_4_4_cry, _3xha_4_5_cry, _3xha_4_5_sum;

  _3xHA_4 _3xha_4_1 (.A(_3xha_4_2_cry), .B(_3xha_4_3_cry), .C(4'b0000), .SUM(CRY[3:0]), .CRY(CRY[7:4]));
  _3xHA_4 _3xha_4_2 (.A(_3xha_4_3_sum), .B(_3xha_4_4_cry), .C(_3xha_4_5_cry), .SUM(SUM[7:4]), .CRY(_3xha_4_2_cry));
  _3xHA_4 _3xha_4_3 (.A(A[7:4]), .B(B[7:4]), .C(C[7:4]), .SUM(_3xha_4_3_sum), .CRY(_3xha_4_3_cry));
  _3xHA_4 _3xha_4_4 (.A(_3xha_4_5_sum), .B(C[3:0]), .C(4'b0000), .SUM(SUM[3:0]), .CRY(_3xha_4_4_cry));
  _3xHA_4 _3xha_4_5 (.A(A[3:0]), .B(B[3:0]), .C(4'b0000), .SUM(_3xha_4_5_sum), .CRY(_3xha_4_5_cry));
endmodule
