// Digital circuit 4xHA-2.dig as structural Verilog
module _4xHA_2 (
  input  [1:0] A,
  input  [1:0] B,
  input  [1:0] C,
  input  [1:0] D,
  output [1:0] SUM,
  output [1:0] CRY
);

  wire fa_1_2_cry, fa_1_3_cry, fa_1_3_sum, fa_1_4_cry, fa_1_4_sum, fa_1_5_cry, fa_1_6_cry, fa_1_6_sum;

  FA_1 fa_1_1 (.A(fa_1_3_cry), .B(fa_1_4_cry), .Cin(fa_1_2_cry), .SUM(CRY[0]), .CRY(CRY[1]));
  FA_1 fa_1_2 (.A(fa_1_3_sum), .B(1'b0), .Cin(D[1]), .SUM(SUM[1]), .CRY(fa_1_2_cry));
  FA_1 fa_1_3 (.A(fa_1_4_sum), .B(fa_1_5_cry), .Cin(fa_1_6_cry), .SUM(fa_1_3_sum), .CRY(fa_1_3_cry));
  FA_1 fa_1_4 (.A(A[1]), .B(B[1]), .Cin(C[1]), .SUM(fa_1_4_sum), .CRY(fa_1_4_cry));
  FA_1 fa_1_5 (.A(fa_1_6_sum), .B(1'b0), .Cin(D[0]), .SUM(SUM[0]), .CRY(fa_1_5_cry));
  FA_1 fa_1_6 (.A(A[0]), .B(B[0]), .Cin(C[0]), .SUM(fa_1_6_sum), .CRY(fa_1_6_cry));
endmodule
