// Digital circuit 4xHA-4.dig as structural Verilog
module _4xHA_4 (
  input  [3:0] A,
  input  [3:0] B,
  input  [3:0] C,
  input  [3:0] D,
  output [3:0] SUM,
  output [3:0] CRY
);

  wire [1:0] _3xha_2_2_cry, _3xha_2_3_cry, _3xha_2_3_sum, _3xha_2_4_cry, _3xha_2_4_sum, _3xha_2_5_cry,
       _3xha_2_6_cry, _3xha_2_6_sum;

  _3xHA_2 _3xha_2_1 (.A(_3xha_2_3_cry), .B(_3xha_2_4_cry), .C(_3xha_2_2_cry), .SUM(CRY[1:0]), .CRY(CRY[3:2]));
  _3xHA_2 _3xha_2_2 (.A(_3xha_2_3_sum), .B(2'b00), .C(D[3:2]), .SUM(SUM[3:2]), .CRY(_3xha_2_2_cry));
  _3xHA_2 _3xha_2_3 (.A(_3xha_2_4_sum), .B(_3xha_2_5_cry), .C(_3xha_2_6_cry), .SUM(_3xha_2_3_sum), .CRY(_3xha_2_3_cry));
  _3xHA_2 _3xha_2_4 (.A(A[3:2]), .B(B[3:2]), .C(C[3:2]), .SUM(_3xha_2_4_sum), .CRY(_3xha_2_4_cry));
  _3xHA_2 _3xha_2_5 (.A(_3xha_2_6_sum), .B(2'b00), .C(D[1:0]), .SUM(SUM[1:0]), .CRY(_3xha_2_5_cry));
  _3xHA_2 _3xha_2_6 (.A(A[1:0]), .B(B[1:0]), .C(C[1:0]), .SUM(_3xha_2_6_sum), .CRY(_3xha_2_6_cry));
endmodule
