// Digital circuit 4xHA-8.dig as structural Verilog
module _4xHA_8 (
  input  [7:0] A,
  input  [7:0] B,
  input  [7:0] C,
  input  [7:0] D,
  output [7:0] SUM,
  output [7:0] CRY
);

  wire [3:0] _3xha_4_2_cry, _3xha_4_3_cry, _3xha_4_3_sum, _3xha_4_4_cry, _3xha_4_4_sum, _3xha_4_5_cry,
       _3xha_4_6_cry, _3xha_4_6_sum;

  _3xHA_4 _3xha_4_1 (.A(_3xha_4_3_cry), .B(_3xha_4_4_cry), .C(_3xha_4_2_cry), .SUM(CRY[3:0]), .CRY(CRY[7:4]));
  _3xHA_4 _3xha_4_2 (.A(_3xha_4_3_sum), .B(4'b0000), .C(D[7:4]), .SUM(SUM[7:4]), .CRY(_3xha_4_2_cry));
  _3xHA_4 _3xha_4_3 (.A(_3xha_4_4_sum), .B(_3xha_4_5_cry), .C(_3xha_4_6_cry), .SUM(_3xha_4_3_sum), .CRY(_3xha_4_3_cry));
  _3xHA_4 _3xha_4_4 (.A(A[7:4]), .B(B[7:4]), .C(C[7:4]), .SUM(_3xha_4_4_sum), .CRY(_3xha_4_4_cry));
  _3xHA_4 _3xha_4_5 (.A(_3xha_4_6_sum), .B(4'b0000), .C(D[3:0]), .SUM(SUM[3:0]), .CRY(_3xha_4_5_cry));
  _3xHA_4 _3xha_4_6 (.A(A[3:0]), .B(B[3:0]), .C(C[3:0]), .SUM(_3xha_4_6_sum), .CRY(_3xha_4_6_cry));
endmodule
