// Digital circuit A_SEL.dig as structural Verilog
module A_SEL (
  input  [7:0] S,
  output Y
);

  wire and_1_out, and_2_out, and_3_out, and_4_out, and_5_out, and_6_out, and_7_out, not_1_out, not_2_out,
       not_3_out, not_4_out, not_5_out, not_6_out, not_7_out, not_8_out;

  not not_1 (not_1_out, S[7]);
  not not_2 (not_2_out, S[6]);
  not not_3 (not_3_out, S[5]);
  not not_4 (not_4_out, S[4]);
  not not_5 (not_5_out, S[3]);
  not not_6 (not_6_out, S[2]);
  not not_7 (not_7_out, S[1]);
  not not_8 (not_8_out, S[0]);
  and and_1 (and_1_out, not_8_out, S[1], not_5_out, not_3_out, not_2_out, not_1_out);
  and and_2 (and_2_out, not_8_out, not_7_out, S[2], not_5_out);
  and and_3 (and_3_out, S[0], not_7_out, not_6_out);
  and and_4 (and_4_out, not_8_out, not_6_out, not_4_out);
  and and_5 (and_5_out, S[1], not_6_out, not_5_out);
  and and_6 (and_6_out, S[1], S[2], not_4_out);
  and and_7 (and_7_out, not_5_out, not_4_out);
  or or_1 (Y, and_1_out, and_2_out, and_3_out, and_4_out, and_5_out, and_6_out, and_7_out);

  // Other names for the same wires on the sheet: S_0 = S[0]; S_1 = S[1]; S_2 = S[2]; S_3 = S[3]; S_4 = S[4];
  //   S_5 = S[5]; S_6 = S[6]; S_7 = S[7]
endmodule
