// Digital circuit BANK_SEL.dig as structural Verilog
module BANK_SEL (
  input  S,
  input  EN,
  output VRAM,
  output GEN
);

  and and_1 (VRAM, EN, S);
  and and_2 (GEN, ~S, EN);  // And
endmodule
