// Digital circuit BNE_SEL.dig as structural Verilog
module BNE_SEL (
  input  [7:0] S,
  output Y
);

  wire not_1_out, not_2_out, not_3_out;

  not not_1 (not_1_out, S[3]);
  not not_2 (not_2_out, S[1]);
  not not_3 (not_3_out, S[0]);
  and and_1 (Y, S[4], not_1_out, S[2], not_2_out, not_3_out);
endmodule
