// Digital circuit BRANCH_SEL.dig as structural Verilog
module BRANCH_SEL (
  input  [7:0] S,
  output Y
);

  wire and_1_out, and_2_out, not_1_out, not_2_out, not_3_out, not_4_out;

  not not_1 (not_1_out, S[3]);
  not not_2 (not_2_out, S[2]);
  not not_3 (not_3_out, S[1]);
  not not_4 (not_4_out, S[0]);
  and and_1 (and_1_out, S[4], not_1_out, S[2], not_3_out, not_4_out);
  and and_2 (and_2_out, S[4], not_1_out, not_2_out, S[1]);
  or or_1 (Y, and_1_out, and_2_out);
endmodule
