// Digital circuit BRK_SEL.dig as structural Verilog
module BRK_SEL (
  input  [15:0] PC,
  input  [15:0] BRK_P,
  input  [15:0] RUNTIME,
  input  [15:0] BRK_R,
  input  STEP,
  input  RUN,
  output Y
);

  wire and_1_out, and_2_out, CLR, not_1_out, not_2_out, or_2_out, xor_1_out;
  wire [15:0] xnor_1_out, xnor_2_out;

  assign xnor_1_out = ~(PC ^ BRK_P);  // XNOr xnor_1, 16 bits wide
  assign xnor_2_out = ~(RUNTIME ^ BRK_R);  // XNOr xnor_2, 16 bits wide
  not not_1 (not_1_out, STEP);
  not not_2 (not_2_out, not_1_out);
  xor xor_1 (xor_1_out, not_2_out, STEP);
  and and_1 (and_1_out, xnor_1_out[0], xnor_1_out[1], xnor_1_out[2], xnor_1_out[3], xnor_1_out[4], xnor_1_out[5], xnor_1_out[6], xnor_1_out[7], xnor_1_out[8], xnor_1_out[9], xnor_1_out[10], xnor_1_out[11], xnor_1_out[12], xnor_1_out[13], xnor_1_out[14], xnor_1_out[15]);
  and and_2 (and_2_out, xnor_2_out[0], xnor_2_out[1], xnor_2_out[2], xnor_2_out[3], xnor_2_out[4], xnor_2_out[5], xnor_2_out[6], xnor_2_out[7], xnor_2_out[8], xnor_2_out[9], xnor_2_out[10], xnor_2_out[11], xnor_2_out[12], xnor_2_out[13], xnor_2_out[14], xnor_2_out[15]);
  or or_1 (CLR, xor_1_out, RUN);
  or or_2 (or_2_out, and_1_out, and_2_out);
  D_FF_AS d_ff_as_1 (.Set(1'b0), .D(1'b1), .C(or_2_out), .Clr(CLR), .Q(Y));  // open: nQ

  // Notes on the sheet:
  //   BRK_P: PC# to break at (output high)
endmodule
