// Digital circuit BS-1.dig as structural Verilog
module BS_1 (
  input  [15:0] A,
  input  S,
  output [15:0] Y,
  output [15:0] R
);

  MUX_1 mux_1_1 (.A(A[15]), .B(1'b0), .A__B(S), .Y(Y[15]));
  MUX_1 mux_1_2 (.A(A[14]), .B(A[15]), .A__B(S), .Y(Y[14]));
  MUX_1 mux_1_3 (.A(A[13]), .B(A[14]), .A__B(S), .Y(Y[13]));
  MUX_1 mux_1_4 (.A(A[12]), .B(A[13]), .A__B(S), .Y(Y[12]));
  MUX_1 mux_1_5 (.A(A[11]), .B(A[12]), .A__B(S), .Y(Y[11]));
  MUX_1 mux_1_6 (.A(A[10]), .B(A[11]), .A__B(S), .Y(Y[10]));
  MUX_1 mux_1_7 (.A(A[9]), .B(A[10]), .A__B(S), .Y(Y[9]));
  MUX_1 mux_1_8 (.A(A[8]), .B(A[9]), .A__B(S), .Y(Y[8]));
  MUX_1 mux_1_9 (.A(A[7]), .B(A[8]), .A__B(S), .Y(Y[7]));
  MUX_1 mux_1_10 (.A(A[6]), .B(A[7]), .A__B(S), .Y(Y[6]));
  MUX_1 mux_1_11 (.A(A[5]), .B(A[6]), .A__B(S), .Y(Y[5]));
  MUX_1 mux_1_12 (.A(A[4]), .B(A[5]), .A__B(S), .Y(Y[4]));
  MUX_1 mux_1_13 (.A(A[3]), .B(A[4]), .A__B(S), .Y(Y[3]));
  MUX_1 mux_1_14 (.A(A[2]), .B(A[3]), .A__B(S), .Y(Y[2]));
  MUX_1 mux_1_15 (.A(A[1]), .B(A[2]), .A__B(S), .Y(Y[1]));
  MUX_1 mux_1_16 (.A(A[0]), .B(A[1]), .A__B(S), .Y(Y[0]));
  MUX_1 mux_1_17 (.A(1'b0), .B(A[0]), .A__B(S), .Y(R[0]));

  assign R[15:1] = {15{1'b0}};
endmodule
