// Digital circuit BUF-16.dig as structural Verilog
module BUF_16 (
  input  [15:0] A,
  input  EN1,
  input  EN2,
  output [15:0] Y
);

  wire and_1_out;

  and and_1 (and_1_out, EN1, EN2);
  assign Y = and_1_out ? A : 16'bz;  // Driver driver_1
endmodule
