// Digital circuit COUNT-16.dig as structural Verilog
module COUNT_16 (
  input  SET,
  input  CLK,
  input  CLR,
  output [15:0] Y
);

  wire jk_ff_as_1_nq, jk_ff_as_2_nq, jk_ff_as_3_nq, jk_ff_as_4_nq, jk_ff_as_5_nq, jk_ff_as_6_nq,
       jk_ff_as_7_nq, jk_ff_as_8_nq, jk_ff_as_9_nq, jk_ff_as_10_nq, jk_ff_as_11_nq, jk_ff_as_12_nq,
       jk_ff_as_13_nq, jk_ff_as_14_nq, jk_ff_as_15_nq, jk_ff_as_16_nq;

  JK_FF_AS jk_ff_as_1 (.Set(SET), .J(1'b1), .C(CLK), .K(1'b1), .Clr(CLR), .Q(Y[0]), .nQ(jk_ff_as_1_nq));
  JK_FF_AS jk_ff_as_2 (.Set(SET), .J(1'b1), .C(jk_ff_as_1_nq), .K(1'b1), .Clr(CLR), .Q(Y[1]), .nQ(jk_ff_as_2_nq));
  JK_FF_AS jk_ff_as_3 (.Set(SET), .J(1'b1), .C(jk_ff_as_2_nq), .K(1'b1), .Clr(CLR), .Q(Y[2]), .nQ(jk_ff_as_3_nq));
  JK_FF_AS jk_ff_as_4 (.Set(SET), .J(1'b1), .C(jk_ff_as_3_nq), .K(1'b1), .Clr(CLR), .Q(Y[3]), .nQ(jk_ff_as_4_nq));
  JK_FF_AS jk_ff_as_5 (.Set(SET), .J(1'b1), .C(jk_ff_as_4_nq), .K(1'b1), .Clr(CLR), .Q(Y[4]), .nQ(jk_ff_as_5_nq));
  JK_FF_AS jk_ff_as_6 (.Set(SET), .J(1'b1), .C(jk_ff_as_5_nq), .K(1'b1), .Clr(CLR), .Q(Y[5]), .nQ(jk_ff_as_6_nq));
  JK_FF_AS jk_ff_as_7 (.Set(SET), .J(1'b1), .C(jk_ff_as_6_nq), .K(1'b1), .Clr(CLR), .Q(Y[6]), .nQ(jk_ff_as_7_nq));
  JK_FF_AS jk_ff_as_8 (.Set(SET), .J(1'b1), .C(jk_ff_as_7_nq), .K(1'b1), .Clr(CLR), .Q(Y[7]), .nQ(jk_ff_as_8_nq));
  JK_FF_AS jk_ff_as_9 (.Set(SET), .J(1'b1), .C(jk_ff_as_8_nq), .K(1'b1), .Clr(CLR), .Q(Y[8]), .nQ(jk_ff_as_9_nq));
  JK_FF_AS jk_ff_as_10 (.Set(SET), .J(1'b1), .C(jk_ff_as_9_nq), .K(1'b1), .Clr(CLR), .Q(Y[9]), .nQ(jk_ff_as_10_nq));
  JK_FF_AS jk_ff_as_11 (.Set(SET), .J(1'b1), .C(jk_ff_as_10_nq), .K(1'b1), .Clr(CLR), .Q(Y[10]), .nQ(jk_ff_as_11_nq));
  JK_FF_AS jk_ff_as_12 (.Set(SET), .J(1'b1), .C(jk_ff_as_11_nq), .K(1'b1), .Clr(CLR), .Q(Y[11]), .nQ(jk_ff_as_12_nq));
  JK_FF_AS jk_ff_as_13 (.Set(SET), .J(1'b1), .C(jk_ff_as_12_nq), .K(1'b1), .Clr(CLR), .Q(Y[12]), .nQ(jk_ff_as_13_nq));
  JK_FF_AS jk_ff_as_14 (.Set(SET), .J(1'b1), .C(jk_ff_as_13_nq), .K(1'b1), .Clr(CLR), .Q(Y[13]), .nQ(jk_ff_as_14_nq));
  JK_FF_AS jk_ff_as_15 (.Set(SET), .J(1'b1), .C(jk_ff_as_14_nq), .K(1'b1), .Clr(CLR), .Q(Y[14]), .nQ(jk_ff_as_15_nq));
  JK_FF_AS jk_ff_as_16 (.Set(SET), .J(1'b1), .C(jk_ff_as_15_nq), .K(1'b1), .Clr(CLR), .Q(Y[15]), .nQ(jk_ff_as_16_nq));
endmodule
