// Digital circuit COUNTAS-16.dig as structural Verilog
module COUNTAS_16 (
  input  [15:0] D,
  input  CLK,
  input  W,
  input  CLR,
  input  SET,
  output [15:0] Y
);

  wire J0, J1, J2, J3, J4, J5, J6, J7, J8, J9, J10, J11, J12, J13, J14, J15, K0, K1, K2, K3, K4, K5, K6, K7,
       K8, K9, K10, K11, K12, K13, K14, K15, mux_1_1_y, mux_1_2_y, mux_1_3_y, mux_1_4_y, mux_1_5_y,
       mux_1_6_y, mux_1_7_y, mux_1_8_y, mux_1_9_y, mux_1_10_y, mux_1_11_y, mux_1_12_y, mux_1_13_y,
       mux_1_14_y, mux_1_15_y, Q0, Q1, Q2, Q3, Q4, Q5, Q6, Q7, Q8, Q9, Q10, Q11, Q12, Q13, Q14, Q15;

  assign {K15, K14, K13, K12, K11, K10, K9, K8, K7, K6, K5, K4, K3, K2, K1, K0} = ~(D & {16{W}});  // NAnd nand_1, 16 bits wide
  assign {J15, J14, J13, J12, J11, J10, J9, J8, J7, J6, J5, J4, J3, J2, J1, J0} = ~({16{W}} & {K15, K14, K13, K12, K11, K10, K9, K8, K7, K6, K5, K4, K3, K2, K1, K0});  // NAnd nand_2, 16 bits wide
  JK_FF_AS jk_ff_as_1 (.Set(SET), .J(J0), .C(CLK), .K(K0), .Clr(CLR), .Q(Y[0]), .nQ(Q0));
  MUX_1 mux_1_1 (.A(Q0), .B(CLK), .A__B(W), .Y(mux_1_1_y));
  JK_FF_AS jk_ff_as_2 (.Set(SET), .J(J1), .C(mux_1_1_y), .K(K1), .Clr(CLR), .Q(Y[1]), .nQ(Q1));
  MUX_1 mux_1_2 (.A(Q1), .B(CLK), .A__B(W), .Y(mux_1_2_y));
  JK_FF_AS jk_ff_as_3 (.Set(SET), .J(J2), .C(mux_1_2_y), .K(K2), .Clr(CLR), .Q(Y[2]), .nQ(Q2));
  MUX_1 mux_1_3 (.A(Q2), .B(CLK), .A__B(W), .Y(mux_1_3_y));
  JK_FF_AS jk_ff_as_4 (.Set(SET), .J(J3), .C(mux_1_3_y), .K(K3), .Clr(CLR), .Q(Y[3]), .nQ(Q3));
  MUX_1 mux_1_4 (.A(Q3), .B(CLK), .A__B(W), .Y(mux_1_4_y));
  JK_FF_AS jk_ff_as_5 (.Set(SET), .J(J4), .C(mux_1_4_y), .K(K4), .Clr(CLR), .Q(Y[4]), .nQ(Q4));
  MUX_1 mux_1_5 (.A(Q4), .B(CLK), .A__B(W), .Y(mux_1_5_y));
  JK_FF_AS jk_ff_as_6 (.Set(SET), .J(J5), .C(mux_1_5_y), .K(K5), .Clr(CLR), .Q(Y[5]), .nQ(Q5));
  MUX_1 mux_1_6 (.A(Q5), .B(CLK), .A__B(W), .Y(mux_1_6_y));
  JK_FF_AS jk_ff_as_7 (.Set(SET), .J(J6), .C(mux_1_6_y), .K(K6), .Clr(CLR), .Q(Y[6]), .nQ(Q6));
  MUX_1 mux_1_7 (.A(Q6), .B(CLK), .A__B(W), .Y(mux_1_7_y));
  JK_FF_AS jk_ff_as_8 (.Set(SET), .J(J7), .C(mux_1_7_y), .K(K7), .Clr(CLR), .Q(Y[7]), .nQ(Q7));
  MUX_1 mux_1_8 (.A(Q7), .B(CLK), .A__B(W), .Y(mux_1_8_y));
  JK_FF_AS jk_ff_as_9 (.Set(SET), .J(J8), .C(mux_1_8_y), .K(K8), .Clr(CLR), .Q(Y[8]), .nQ(Q8));
  MUX_1 mux_1_9 (.A(Q8), .B(CLK), .A__B(W), .Y(mux_1_9_y));
  JK_FF_AS jk_ff_as_10 (.Set(SET), .J(J9), .C(mux_1_9_y), .K(K9), .Clr(CLR), .Q(Y[9]), .nQ(Q9));
  MUX_1 mux_1_10 (.A(Q9), .B(CLK), .A__B(W), .Y(mux_1_10_y));
  JK_FF_AS jk_ff_as_11 (.Set(SET), .J(J10), .C(mux_1_10_y), .K(K10), .Clr(CLR), .Q(Y[10]), .nQ(Q10));
  MUX_1 mux_1_11 (.A(Q10), .B(CLK), .A__B(W), .Y(mux_1_11_y));
  JK_FF_AS jk_ff_as_12 (.Set(SET), .J(J11), .C(mux_1_11_y), .K(K11), .Clr(CLR), .Q(Y[11]), .nQ(Q11));
  MUX_1 mux_1_12 (.A(Q11), .B(CLK), .A__B(W), .Y(mux_1_12_y));
  JK_FF_AS jk_ff_as_13 (.Set(SET), .J(J12), .C(mux_1_12_y), .K(K12), .Clr(CLR), .Q(Y[12]), .nQ(Q12));
  MUX_1 mux_1_13 (.A(Q12), .B(CLK), .A__B(W), .Y(mux_1_13_y));
  JK_FF_AS jk_ff_as_14 (.Set(SET), .J(J13), .C(mux_1_13_y), .K(K13), .Clr(CLR), .Q(Y[13]), .nQ(Q13));
  MUX_1 mux_1_14 (.A(Q13), .B(CLK), .A__B(W), .Y(mux_1_14_y));
  JK_FF_AS jk_ff_as_15 (.Set(SET), .J(J14), .C(mux_1_14_y), .K(K14), .Clr(CLR), .Q(Y[14]), .nQ(Q14));
  MUX_1 mux_1_15 (.A(Q14), .B(CLK), .A__B(W), .Y(mux_1_15_y));
  JK_FF_AS jk_ff_as_16 (.Set(SET), .J(J15), .C(mux_1_15_y), .K(K15), .Clr(CLR), .Q(Y[15]), .nQ(Q15));

  // Other names for the same wires on the sheet: DATA[15:0] = D; W0 = W; W_t[15:0] = {16{W}}
endmodule
