// Digital circuit CRAM-16.dig as structural Verilog
module CRAM_16 (
  input  [15:0] A,
  input  CLK,
  input  [15:0] DIN,
  input  STR,
  input  LD,
  input  B,
  output [15:0] D
);

  wire LD_R, LD_t, LD_V, STR_R, STR_V;
  wire [15:0] D_t, driver_2_out, driverinvsel_1_out;

  and and_1 (LD_t, LD, ~STR);  // And
  assign D_t = STR ? DIN : 16'bz;  // Driver driver_1
  assign driver_2_out = A[15] ? A : 16'bz;  // Driver driver_2
  assign driverinvsel_1_out = ~A[15] ? A : 16'bz;  // DriverInvSel driverinvsel_1
  GraphicCard #(.graphicHeight(16), .graphicWidth(16), .Bits(16)) graphiccard_1 (
    .A(driver_2_out[8:0]), .str(STR_V), .C(CLK), .ld(LD_V), .B(B), .D(D_t));
  RAMSinglePort #(.AddrBits(16), .Bits(16)) ramsingleport_1 (
    .A(driverinvsel_1_out), .str(STR_R), .C(CLK), .ld(LD_R), .D(D_t));
  and and_2 (STR_V, STR, A[15]);
  and and_3 (STR_R, ~A[15], STR);  // And
  and and_4 (LD_V, LD_t, A[15]);
  and and_5 (LD_R, ~A[15], LD_t);  // And
  assign D = LD_t ? D_t : 16'bz;  // Driver driver_3

  // Other names for the same wires on the sheet: VRAM__RAM = A[15]; C = CLK

  // Notes on the sheet:
  //   A < 0x8000 ->  RAM
  //   A >= 0x8000 -> VRAM1
  //   A >= 0x8100 -> VRAM2
endmodule
