// Digital circuit DEC-3C.dig as structural Verilog
module DEC_3C (
  input  [2:0] S,
  input  EN,
  output [7:0] Y
);

  wire not_1_out, not_2_out, not_3_out;

  not not_1 (not_1_out, S[1]);
  not not_2 (not_2_out, S[2]);
  not not_3 (not_3_out, S[0]);
  and and_1 (Y[0], not_3_out, not_1_out, EN, not_2_out);
  and and_2 (Y[1], S[0], not_1_out, EN, not_2_out);
  and and_3 (Y[2], not_3_out, S[1], EN, not_2_out);
  and and_4 (Y[3], S[0], S[1], EN, not_2_out);
  and and_5 (Y[4], not_3_out, not_1_out, EN, S[2]);
  and and_6 (Y[5], S[0], not_1_out, EN, S[2]);
  and and_7 (Y[6], not_3_out, S[1], EN, S[2]);
  and and_8 (Y[7], S[0], S[1], EN, S[2]);
endmodule
