// Digital circuit DEC-4.dig as structural Verilog
module DEC_4 (
  input  [3:0] S,
  input  EN,
  output Y15,
  output Y14,
  output Y13,
  output Y12,
  output Y11,
  output Y10,
  output Y9,
  output Y8,
  output Y7,
  output Y6,
  output Y5,
  output Y4,
  output Y3,
  output Y2,
  output Y1,
  output Y0
);

  wire not_1_out, not_2_out, not_3_out, not_4_out;

  not not_1 (not_1_out, S[3]);
  not not_2 (not_2_out, S[1]);
  not not_3 (not_3_out, S[2]);
  not not_4 (not_4_out, S[0]);
  and and_1 (Y0, not_4_out, not_2_out, EN, not_3_out, not_1_out);
  and and_2 (Y1, S[0], not_2_out, EN, not_3_out, not_1_out);
  and and_3 (Y2, not_4_out, S[1], EN, not_3_out, not_1_out);
  and and_4 (Y3, S[0], S[1], EN, not_3_out, not_1_out);
  and and_5 (Y4, not_4_out, not_2_out, EN, S[2], not_1_out);
  and and_6 (Y5, S[0], not_2_out, EN, S[2], not_1_out);
  and and_7 (Y6, not_4_out, S[1], EN, S[2], not_1_out);
  and and_8 (Y7, S[0], S[1], EN, S[2], not_1_out);
  and and_9 (Y8, not_4_out, not_2_out, EN, not_3_out, S[3]);
  and and_10 (Y9, S[0], not_2_out, EN, not_3_out, S[3]);
  and and_11 (Y10, not_4_out, S[1], EN, not_3_out, S[3]);
  and and_12 (Y11, S[0], S[1], EN, not_3_out, S[3]);
  and and_13 (Y12, not_4_out, not_2_out, EN, S[2], S[3]);
  and and_14 (Y13, S[0], not_2_out, EN, S[2], S[3]);
  and and_15 (Y14, not_4_out, S[1], EN, S[2], S[3]);
  and and_16 (Y15, S[0], S[1], EN, S[2], S[3]);
endmodule
