// Digital circuit DEC-4C.dig as structural Verilog
module DEC_4C (
  input  [3:0] S,
  input  EN,
  output [15:0] Y
);

  wire not_1_out, not_2_out, not_3_out, not_4_out;

  not not_1 (not_1_out, S[3]);
  not not_2 (not_2_out, S[1]);
  not not_3 (not_3_out, S[2]);
  not not_4 (not_4_out, S[0]);
  and and_1 (Y[0], not_4_out, not_2_out, EN, not_3_out, not_1_out);
  and and_2 (Y[1], S[0], not_2_out, EN, not_3_out, not_1_out);
  and and_3 (Y[2], not_4_out, S[1], EN, not_3_out, not_1_out);
  and and_4 (Y[3], S[0], S[1], EN, not_3_out, not_1_out);
  and and_5 (Y[4], not_4_out, not_2_out, EN, S[2], not_1_out);
  and and_6 (Y[5], S[0], not_2_out, EN, S[2], not_1_out);
  and and_7 (Y[6], not_4_out, S[1], EN, S[2], not_1_out);
  and and_8 (Y[7], S[0], S[1], EN, S[2], not_1_out);
  and and_9 (Y[8], not_4_out, not_2_out, EN, not_3_out, S[3]);
  and and_10 (Y[9], S[0], not_2_out, EN, not_3_out, S[3]);
  and and_11 (Y[10], not_4_out, S[1], EN, not_3_out, S[3]);
  and and_12 (Y[11], S[0], S[1], EN, not_3_out, S[3]);
  and and_13 (Y[12], not_4_out, not_2_out, EN, S[2], S[3]);
  and and_14 (Y[13], S[0], not_2_out, EN, S[2], S[3]);
  and and_15 (Y[14], not_4_out, S[1], EN, S[2], S[3]);
  and and_16 (Y[15], S[0], S[1], EN, S[2], S[3]);
  // Pins of 1 and 16 bits meet at Y
endmodule
