// Digital circuit DIV(bugged, counter).dig as structural Verilog
module DIV_bugged__counter (
  input  [15:0] BASE,
  input  [15:0] DIV,
  input  CLK_EN,
  input  RESTART,
  input  CLK,
  input  CLK_STEP,
  input  clk_2,
  output [15:0] out_4,
  output [15:0] out_6,
  output [15:0] out_7,
  output [15:0] out_10,
  output [15:0] out_12
);

  wire and_1_out, d_ff_as_1_nq, d_ff_as_1_q, DONE, mux_1_1_y, mux_1_2_y, or_1_out;
  wire [15:0] driver_1_out, neg_not_1_p4;

  MUX_1 mux_1_1 (.A(1'b0), .B(clk_2), .A__B(CLK_EN), .Y(mux_1_1_y));
  MUX_1 mux_1_2 (.A(mux_1_1_y), .B(CLK), .A__B(CLK_STEP), .Y(mux_1_2_y));
  and and_1 (and_1_out, mux_1_2_y, DONE);
  D_FF_AS d_ff_as_1 (.Set(1'b0), .D(1'b1), .C(and_1_out), .Clr(RESTART), .Q(d_ff_as_1_q), .nQ(d_ff_as_1_nq));
  assign driver_1_out = d_ff_as_1_nq ? BASE : 16'bz;  // Driver driver_1
  // NEG_NOT neg_not_1: pin names not known; wires that end beside it: DIV, d_ff_as_1_q, 1'b1, neg_not_1_p4
  Register #(.Bits(16)) register_1 (.D(driver_1_out), .C(and_1_out), .en(1'b1), .Q(out_12));
  assign driver_1_out = d_ff_as_1_q ? out_7 : 16'bz;  // Driver driver_2
  FA_16 fa_16_1 (.A(out_12), .B(neg_not_1_p4), .CIN(1'b0), .SUM(out_7));  // open: CRY
  or or_1 (or_1_out, and_1_out, RESTART);
  not not_1 (DONE, out_7[15]);
  Counter #(.Bits(16)) counter_1 (.en(1'b1), .C(or_1_out), .clr(RESTART), .out(out_10));  // open: ovf
  Register #(.Bits(16)) register_2 (.D(out_7), .C(and_1_out), .en(1'b1), .Q(out_4));
  FA_16 fa_16_2 (.A(out_10), .B({16{1'b1}}), .CIN(1'b0), .SUM(out_6));  // open: CRY

  // Notes on the sheet:
  //   clk_2: Hz: 5
endmodule
