// Digital circuit DIV-16C.dig as structural Verilog
module DIV_16C (
  input  [15:0] B,
  input  [15:0] D,
  input  CLR,
  input  CLK_EN,
  input  CLK,
  input  CLK_STEP,
  input  clk_2,
  output [15:0] R,
  output INTERUPT,
  output B__eq__D,
  output B__lt__D,
  output D__eq__1,
  output D__eq__0,
  output D__eq__2,
  output NRM,
  output ERR,
  output [15:0] Q
);

  wire and_1_out, d_ff_as_1_nq, d_ff_as_1_q, mux_1_1_y, mux_1_2_y, or_1_out;
  wire [15:0] add_2_s, bs_1_1_r, bs_1_1_y, count_16_1_y, d_ff_as_3_q, neg_not_1_p4, register_1_q, xnor_1_out,
       xnor_2_out;
  wire [15:1] slt_16_1_eq, slt_16_1_lt;
  wire [16:0] add_1_s, d_ff_as_2_q, driver_1_out;

  MUX_1 mux_1_1 (.A(1'b0), .B(clk_2), .A__B(CLK_EN), .Y(mux_1_1_y));
  MUX_1 mux_1_2 (.A(mux_1_1_y), .B(CLK), .A__B(CLK_STEP), .Y(mux_1_2_y));
  and and_1 (and_1_out, mux_1_2_y, INTERUPT);
  assign xnor_1_out = ~(16'h2 ^ D);  // XNOr xnor_1, 16 bits wide
  D_FF_AS d_ff_as_1 (.Set(1'b0), .D(1'b1), .C(and_1_out), .Clr(CLR), .Q(d_ff_as_1_q), .nQ(d_ff_as_1_nq));
  and and_2 (D__eq__2, xnor_1_out[8], xnor_1_out[15], xnor_1_out[14], xnor_1_out[13], xnor_1_out[12], xnor_1_out[11], xnor_1_out[10], xnor_1_out[9], xnor_1_out[7], xnor_1_out[6], xnor_1_out[5], xnor_1_out[4], xnor_1_out[3], xnor_1_out[2], xnor_1_out[1], xnor_1_out[0]);
  assign driver_1_out = d_ff_as_1_nq ? {1'b0, B} : 17'bz;  // Driver driver_1
  D_FF_AS #(.Bits(17)) d_ff_as_2 (.Set(1'b0), .D(driver_1_out), .C(and_1_out), .Clr(CLR), .Q(d_ff_as_2_q));  // open: nQ
  // NEG_NOT neg_not_1: pin names not known; wires that end beside it: D, d_ff_as_1_q, 1'b1, neg_not_1_p4
  nor nor_1 (D__eq__0, D[8], D[15], D[14], D[13], D[12], D[11], D[10], D[9], D[7], D[6], D[5], D[4], D[3], D[2], D[1], D[0]);
  assign xnor_2_out = ~(16'h1 ^ D);  // XNOr xnor_2, 16 bits wide
  assign driver_1_out = d_ff_as_1_q ? add_1_s : 17'bz;  // Driver driver_2
  Add #(.Bits(17)) add_1 (.a(d_ff_as_2_q), .b({1'b1, neg_not_1_p4}), .c_i(1'b0), .s(add_1_s));  // open: c_o
  and and_3 (D__eq__1, xnor_2_out[8], xnor_2_out[15], xnor_2_out[14], xnor_2_out[13], xnor_2_out[12], xnor_2_out[11], xnor_2_out[10], xnor_2_out[9], xnor_2_out[7], xnor_2_out[6], xnor_2_out[5], xnor_2_out[4], xnor_2_out[3], xnor_2_out[2], xnor_2_out[1], xnor_2_out[0]);
  D_FF_AS #(.Bits(17)) d_ff_as_3 (
    .Set(1'b0), .D(add_1_s), .C(~and_1_out), .Clr(CLR), .Q({NRM, d_ff_as_3_q}));  // open: nQ
  or or_1 (or_1_out, and_1_out, CLR);
  SLT_16 slt_16_1 (.A(B), .B(D), .LT({slt_16_1_lt, B__lt__D}), .EQ({slt_16_1_eq, B__eq__D}));
  COUNT_16 count_16_1 (.EN(1'b1), .INC(or_1_out), .CLR(CLR), .Y(count_16_1_y));
  Add #(.Bits(16)) add_2 (.a(count_16_1_y), .b({16{1'b1}}), .c_i(1'b0), .s(add_2_s));  // open: c_o
  Register #(.Bits(16)) register_1 (.D(d_ff_as_3_q), .C(and_1_out), .en(1'b1), .Q(register_1_q));
  nor nor_2 (INTERUPT, NRM, D__eq__2, B__lt__D, B__eq__D, D__eq__1, D__eq__0);
  BS_1 bs_1_1 (.A(B), .S(D__eq__2), .Y(bs_1_1_y), .R(bs_1_1_r));
  DIV_SEL div_sel_1 (
    .D_eq_0({16{1'b0}}), .D_eq_1({16{1'b0}}), .B_eq_D({16{1'b0}}), .B_lt_D(B), .D_eq_2(bs_1_1_r),
    .NRM(register_1_q), .SEL({D__eq__0, D__eq__1, B__eq__D, B__lt__D, D__eq__2}), .Y(R));
  DIV_SEL div_sel_2 (
    .D_eq_0({16{1'b0}}), .D_eq_1(B), .B_eq_D(16'h1), .B_lt_D({16{1'b0}}), .D_eq_2(bs_1_1_y), .NRM(add_2_s),
    .SEL({D__eq__0, D__eq__1, B__eq__D, B__lt__D, D__eq__2}), .Y(Q));

  assign ERR = D__eq__0;

  // Other names for the same wires on the sheet: WORKING = INTERUPT

  // Notes on the sheet:
  //   clk_2: Hz: 5
  //   splitters convert 16 into 17 to prevent
  //   false finish flags at numbers >= 2^15
  //   TODO
  //   - find better way to decrement quotient
  //   - find better flag system that does not require
  //   trasforming numbers to 17 bits
  //   - implement lookahead fa
  //   - implement own reg
  //   - maybe set final R reg to clr input???
  //   - get jk to work that would be nice lol
  //   most of these flags are probably not worth the hardware
  //   also i hate this, its devolved into caos
  //   clock input is inverted to prevent junk data
  //    from trigering finish check
  //   counter, that tracks quotient, 
  //   fa decrements by one
endmodule
