// Digital circuit DIV-16V1.dig as structural Verilog
module DIV_16V1 (
  input  [15:0] B,
  input  [15:0] D,
  input  CLK,
  input  CLR,
  output [15:0] Q,
  output [16:0] R
);

  wire d_ff_as_1_nq, d_ff_as_1_q, DONE, or_1_out;
  wire [15:0] counter_1_out, neg_not_1_p4;
  wire [16:0] add_1_s, d_ff_as_2_q, d_ff_as_3_q, driver_1_out;

  D_FF_AS d_ff_as_1 (.Set(1'b0), .D(1'b1), .C(CLK), .Clr(CLR), .Q(d_ff_as_1_q), .nQ(d_ff_as_1_nq));
  assign driver_1_out = d_ff_as_1_nq ? {1'b0, B} : 17'bz;  // Driver driver_1
  D_FF_AS #(.Bits(17)) d_ff_as_2 (.Set(1'b0), .D(driver_1_out), .C(CLK), .Clr(CLR), .Q(d_ff_as_2_q));  // open: nQ
  // NEG_NOT neg_not_1: pin names not known; wires that end beside it: D, d_ff_as_1_q, 1'b1, neg_not_1_p4
  assign driver_1_out = d_ff_as_1_q ? add_1_s : 17'bz;  // Driver driver_2
  Add #(.Bits(17)) add_1 (.a(d_ff_as_2_q), .b({1'b1, neg_not_1_p4}), .c_i(1'b0), .s(add_1_s));  // open: c_o
  D_FF_AS #(.Bits(17)) d_ff_as_3 (.Set(1'b0), .D(add_1_s), .C(~CLK), .Clr(CLR), .Q(d_ff_as_3_q));  // open: nQ
  or or_1 (or_1_out, CLK, CLR);
  not not_1 (DONE, d_ff_as_3_q[16]);
  Counter #(.Bits(16)) counter_1 (.en(1'b1), .C(or_1_out), .clr(CLR), .out(counter_1_out));  // open: ovf
  Register #(.Bits(17)) register_1 (.D(d_ff_as_3_q), .C(CLK), .en(1'b1), .Q(R));
  Add #(.Bits(16)) add_2 (.a(counter_1_out), .b({16{1'b1}}), .c_i(1'b0), .s(Q));  // open: c_o

  // Notes on the sheet:
  //   splitters convert 16 into 17 to prevent
  //   false finish flags at numbers >= 2^15
  //   TODO
  //   - find better way to decrement quotient
  //   - find better flag system that does not require
  //   trasforming numbers to 17 bits
  //   - implement lookahead fa
  //   - implement own reg
  //   - maybe set final R reg to clr input???
  //   - varios flags, /0, /1 , x/x etc. check phone for full list
  //   - get jk to work that would be nice lol
  //   clock input is inverted to prevent junk data
  //    from trigering finish check
  //   counter, that tracks quotient, 
  //   fa decrements by one
endmodule
