// Digital circuit DIV-SEL.dig as structural Verilog
module DIV_SEL (
  input  [15:0] D_eq_0,
  input  [15:0] D_eq_1,
  input  [15:0] B_eq_D,
  input  [15:0] B_lt_D,
  input  [15:0] D_eq_2,
  input  [15:0] NRM,
  input  [4:0] SEL,
  output [15:0] Y
);

  wire and_1_out, and_2_out, and_3_out, and_4_out, not_1_out, not_2_out, not_3_out, not_4_out, or_1_out,
       or_2_out, or_3_out;
  wire [15:0] mux_16_1_y, mux_16_2_y, mux_16_3_y, mux_16_4_y, mux_16_5_y, mux_16_6_y;

  not not_1 (not_1_out, SEL[4]);
  not not_2 (not_2_out, SEL[3]);
  not not_3 (not_3_out, SEL[2]);
  not not_4 (not_4_out, SEL[1]);
  or or_1 (or_1_out, SEL[4], SEL[3]);
  and and_1 (and_1_out, SEL[1], not_1_out, not_2_out);
  and and_2 (and_2_out, SEL[2], not_1_out, not_2_out);
  and and_3 (and_3_out, SEL[0], not_4_out, not_2_out);
  and and_4 (and_4_out, SEL[2], not_2_out);
  or or_2 (or_2_out, and_1_out, and_2_out);
  or or_3 (or_3_out, and_3_out, and_4_out, SEL[4]);
  MUX_16 mux_16_1 (.A(NRM), .B(D_eq_2), .A__B(or_3_out), .Y(mux_16_1_y));
  MUX_16 mux_16_2 (.A(B_lt_D), .B(B_eq_D), .A__B(or_3_out), .Y(mux_16_2_y));
  MUX_16 mux_16_3 (.A(D_eq_1), .B(D_eq_0), .A__B(or_3_out), .Y(mux_16_3_y));
  MUX_16 mux_16_4 (.A({16{1'b0}}), .B({16{1'b0}}), .A__B(or_3_out), .Y(mux_16_4_y));
  MUX_16 mux_16_5 (.A(mux_16_1_y), .B(mux_16_2_y), .A__B(or_2_out), .Y(mux_16_5_y));
  MUX_16 mux_16_6 (.A(mux_16_3_y), .B(mux_16_4_y), .A__B(or_2_out), .Y(mux_16_6_y));
  MUX_16 mux_16_7 (.A(mux_16_5_y), .B(mux_16_6_y), .A__B(or_1_out), .Y(Y));

  // Notes on the sheet:
  //   msb to lsb is
  //   D=0, D=1, B=D, B<D, D=2
endmodule
