// Digital circuit DIV-16.dig as structural Verilog
module DIV_16 (
  input  [15:0] B,
  input  [15:0] D,
  input  CLK,
  input  INIT,
  output [15:0] R,
  output [15:0] Q,
  output W
);

  wire and_1_out, and_2_out, d_ff_as_1_nq, d_ff_as_1_q, not_1_out, or_1_out;
  wire [15:0] not__neg_1_y, pc_16_1_q;
  wire [16:0] d_ff_as_2_q, d_ff_as_3_q, driver_1_out, fa_17_1_sum;

  and and_1 (and_1_out, CLK, W);
  and and_2 (and_2_out, ~INIT, and_1_out);  // And
  D_FF_AS d_ff_as_1 (.Set(1'b0), .D(1'b1), .C(and_2_out), .Clr(INIT), .Q(d_ff_as_1_q), .nQ(d_ff_as_1_nq));
  assign driver_1_out = d_ff_as_1_nq ? {1'b0, B} : 17'bz;  // Driver driver_1
  D_FF_AS #(.Bits(17)) d_ff_as_2 (
    .Set(1'b0), .D(driver_1_out), .C(and_2_out), .Clr(INIT), .Q(d_ff_as_2_q));  // open: nQ
  NOT__NEG not__neg_1 (.A(D), .PASS(d_ff_as_1_q), .NOT__NEG(1'b1), .Y(not__neg_1_y));  // open: CRY
  assign driver_1_out = d_ff_as_1_q ? fa_17_1_sum : 17'bz;  // Driver driver_2
  FA_17 fa_17_1 (.A(d_ff_as_2_q), .B({1'b1, not__neg_1_y}), .Cin(1'b0), .SUM(fa_17_1_sum));  // open: CRY
  D_FF_AS #(.Bits(17)) d_ff_as_3 (
    .Set(1'b0), .D(fa_17_1_sum), .C(~and_2_out), .Clr(INIT), .Q(d_ff_as_3_q));  // open: nQ
  or or_1 (or_1_out, and_2_out, INIT);
  not not_1 (not_1_out, or_1_out);
  not not_2 (W, d_ff_as_3_q[16]);
  PC_16 pc_16_1 (
    .D({16{1'b0}}), .CLK(not_1_out), .W(1'b0), .B_EN(1'b0), .A_EN(1'b0), .CLR(INIT), .SET(1'b0), .INC(1'b1),
    .Q(pc_16_1_q));  // open: B, A
  D_FF #(.Bits(16)) d_ff_1 (.D(d_ff_as_3_q[15:0]), .C(and_2_out), .Q(R));  // open: nQ
  FA_16 fa_16_1 (.A(pc_16_1_q), .B({16{1'b1}}), .CIN(1'b0), .SUM(Q));  // open: CRY

  // Other names for the same wires on the sheet: WORKING = W

  // Notes on the sheet:
  //   INIT: must be high to initalize circuit before (or at?) first clock
  //   splitters convert 16 into 17 to prevent
  //   false finish flags at numbers >= 2^15
  //   TODO
  //   - find better way to decrement quotient
  //   - find better flag system that does not require
  //   trasforming numbers to 17 bits
  //   - implement lookahead fa
  //   clock input is inverted to prevent junk data
  //    from trigering finish check
  //   counter, that tracks quotient, 
  //   fa decrements by one
endmodule
