// Digital circuit FA-1.dig as structural Verilog
module FA_1 (
  input  A,
  input  B,
  input  Cin,
  output SUM,
  output CRY
);

  wire and_1_out, and_2_out, xor_1_out;

  xor xor_1 (xor_1_out, A, B);
  xor xor_2 (SUM, xor_1_out, Cin);
  and and_1 (and_1_out, xor_1_out, Cin);
  and and_2 (and_2_out, B, A);
  or or_1 (CRY, and_1_out, and_2_out);
endmodule
