// Digital circuit FA-17.dig as structural Verilog
module FA_17 (
  input  [16:0] A,
  input  [16:0] B,
  input  Cin,
  output [16:0] SUM,
  output CRY
);

  wire fa_1_2_cry, fa_1_3_cry, fa_1_4_cry, fa_1_5_cry, fa_1_6_cry, fa_1_7_cry, fa_1_8_cry, fa_1_9_cry,
       fa_1_10_cry, fa_1_11_cry, fa_1_12_cry, fa_1_13_cry, fa_1_14_cry, fa_1_15_cry, fa_1_16_cry, fa_1_17_cry;

  FA_1 fa_1_1 (.A(A[16]), .B(B[16]), .Cin(fa_1_2_cry), .SUM(SUM[16]), .CRY(CRY));
  FA_1 fa_1_2 (.A(A[15]), .B(B[15]), .Cin(fa_1_3_cry), .SUM(SUM[15]), .CRY(fa_1_2_cry));
  FA_1 fa_1_3 (.A(A[14]), .B(B[14]), .Cin(fa_1_4_cry), .SUM(SUM[14]), .CRY(fa_1_3_cry));
  FA_1 fa_1_4 (.A(A[13]), .B(B[13]), .Cin(fa_1_5_cry), .SUM(SUM[13]), .CRY(fa_1_4_cry));
  FA_1 fa_1_5 (.A(A[12]), .B(B[12]), .Cin(fa_1_6_cry), .SUM(SUM[12]), .CRY(fa_1_5_cry));
  FA_1 fa_1_6 (.A(A[11]), .B(B[11]), .Cin(fa_1_7_cry), .SUM(SUM[11]), .CRY(fa_1_6_cry));
  FA_1 fa_1_7 (.A(A[10]), .B(B[10]), .Cin(fa_1_8_cry), .SUM(SUM[10]), .CRY(fa_1_7_cry));
  FA_1 fa_1_8 (.A(A[9]), .B(B[9]), .Cin(fa_1_9_cry), .SUM(SUM[9]), .CRY(fa_1_8_cry));
  FA_1 fa_1_9 (.A(A[8]), .B(B[8]), .Cin(fa_1_10_cry), .SUM(SUM[8]), .CRY(fa_1_9_cry));
  FA_1 fa_1_10 (.A(A[7]), .B(B[7]), .Cin(fa_1_11_cry), .SUM(SUM[7]), .CRY(fa_1_10_cry));
  FA_1 fa_1_11 (.A(A[6]), .B(B[6]), .Cin(fa_1_12_cry), .SUM(SUM[6]), .CRY(fa_1_11_cry));
  FA_1 fa_1_12 (.A(A[5]), .B(B[5]), .Cin(fa_1_13_cry), .SUM(SUM[5]), .CRY(fa_1_12_cry));
  FA_1 fa_1_13 (.A(A[4]), .B(B[4]), .Cin(fa_1_14_cry), .SUM(SUM[4]), .CRY(fa_1_13_cry));
  FA_1 fa_1_14 (.A(A[3]), .B(B[3]), .Cin(fa_1_15_cry), .SUM(SUM[3]), .CRY(fa_1_14_cry));
  FA_1 fa_1_15 (.A(A[2]), .B(B[2]), .Cin(fa_1_16_cry), .SUM(SUM[2]), .CRY(fa_1_15_cry));
  FA_1 fa_1_16 (.A(A[1]), .B(B[1]), .Cin(fa_1_17_cry), .SUM(SUM[1]), .CRY(fa_1_16_cry));
  FA_1 fa_1_17 (.A(A[0]), .B(B[0]), .Cin(Cin), .SUM(SUM[0]), .CRY(fa_1_17_cry));
endmodule
