// Digital circuit FA-2.dig as structural Verilog
module FA_2 (
  input  [1:0] A,
  input  [1:0] B,
  input  Cin,
  output [1:0] SUM,
  output [1:0] CRY
);

  wire fa_1_2_cry;

  FA_1 fa_1_1 (.A(A[1]), .B(B[1]), .Cin(fa_1_2_cry), .SUM(SUM[1]), .CRY(CRY[0]));
  FA_1 fa_1_2 (.A(A[0]), .B(B[0]), .Cin(Cin), .SUM(SUM[0]), .CRY(fa_1_2_cry));

  assign CRY[1] = 1'b0;
endmodule
