// Digital circuit INC-16.dig as structural Verilog
module INC_16 (
  input  [15:0] A,
  input  INC,
  output [15:0] Y,
  output CRY
);

  wire ha_1_1_cry, ha_1_2_cry, ha_1_3_cry, ha_1_4_cry, ha_1_5_cry, ha_1_6_cry, ha_1_7_cry, ha_1_8_cry,
       ha_1_9_cry, ha_1_10_cry, ha_1_11_cry, ha_1_12_cry, ha_1_14_cry, ha_1_15_cry, ha_1_16_cry;

  HA_1 ha_1_1 (.A(A[3]), .B(ha_1_2_cry), .SUM(Y[3]), .CRY(ha_1_1_cry));
  HA_1 ha_1_2 (.A(A[2]), .B(ha_1_3_cry), .SUM(Y[2]), .CRY(ha_1_2_cry));
  HA_1 ha_1_3 (.A(A[1]), .B(ha_1_4_cry), .SUM(Y[1]), .CRY(ha_1_3_cry));
  HA_1 ha_1_4 (.A(A[0]), .B(INC), .SUM(Y[0]), .CRY(ha_1_4_cry));
  HA_1 ha_1_5 (.A(A[7]), .B(ha_1_6_cry), .SUM(Y[7]), .CRY(ha_1_5_cry));
  HA_1 ha_1_6 (.A(A[6]), .B(ha_1_7_cry), .SUM(Y[6]), .CRY(ha_1_6_cry));
  HA_1 ha_1_7 (.A(A[5]), .B(ha_1_8_cry), .SUM(Y[5]), .CRY(ha_1_7_cry));
  HA_1 ha_1_8 (.A(A[4]), .B(ha_1_1_cry), .SUM(Y[4]), .CRY(ha_1_8_cry));
  HA_1 ha_1_9 (.A(A[11]), .B(ha_1_10_cry), .SUM(Y[11]), .CRY(ha_1_9_cry));
  HA_1 ha_1_10 (.A(A[10]), .B(ha_1_11_cry), .SUM(Y[10]), .CRY(ha_1_10_cry));
  HA_1 ha_1_11 (.A(A[9]), .B(ha_1_12_cry), .SUM(Y[9]), .CRY(ha_1_11_cry));
  HA_1 ha_1_12 (.A(A[8]), .B(ha_1_5_cry), .SUM(Y[8]), .CRY(ha_1_12_cry));
  HA_1 ha_1_13 (.A(A[15]), .B(ha_1_14_cry), .SUM(Y[15]), .CRY(CRY));
  HA_1 ha_1_14 (.A(A[14]), .B(ha_1_15_cry), .SUM(Y[14]), .CRY(ha_1_14_cry));
  HA_1 ha_1_15 (.A(A[13]), .B(ha_1_16_cry), .SUM(Y[13]), .CRY(ha_1_15_cry));
  HA_1 ha_1_16 (.A(A[12]), .B(ha_1_9_cry), .SUM(Y[12]), .CRY(ha_1_16_cry));
endmodule
