// Digital circuit INIT.dig as structural Verilog
module INIT (
  input  A,
  output Y
);

  wire d_ff_1_q, not_1_out, not_2_out;

  D_FF d_ff_1 (.D(1'b1), .C(A), .Q(d_ff_1_q));  // open: nQ
  not not_1 (not_1_out, not_2_out);
  not not_2 (not_2_out, d_ff_1_q);
  xor xor_1 (Y, not_1_out, d_ff_1_q);
endmodule
