// Digital circuit JK-CLR.dig as structural Verilog
module JK_CLR (
  input  J,
  input  K,
  input  CLK,
  input  PRE,
  input  CLR,
  output Q,
  output Q_2
);

  wire delay_1_out, nand_1_out, nand_2_out, nand_3_out, nand_4_out, nand_5_out, nand_6_out, not_1_out;

  nand nand_1 (nand_1_out, Q_2, J, CLK);
  nand nand_2 (nand_2_out, CLK, K, Q);
  not not_1 (not_1_out, CLK);
  Delay #(.delayTime(10)) delay_1 (.in(not_1_out), .out(delay_1_out));
  nand nand_3 (nand_3_out, ~PRE, nand_1_out, nand_4_out);  // NAnd
  nand nand_4 (nand_4_out, nand_3_out, nand_2_out, ~CLR);  // NAnd
  nand nand_5 (nand_5_out, nand_3_out, not_1_out);
  nand nand_6 (nand_6_out, not_1_out, nand_4_out);
  nand nand_7 (Q, Q_2, nand_5_out);
  nand nand_8 (Q_2, nand_6_out, Q);
endmodule
