// Digital circuit JMP_SEL.dig as structural Verilog
module JMP_SEL (
  input  [7:0] S,
  output Y
);

  wire and_1_out, and_2_out, not_1_out;

  not not_1 (not_1_out, S[3]);
  and and_1 (and_1_out, S[4], not_1_out, S[2], S[0]);
  and and_2 (and_2_out, S[4], not_1_out, S[2], S[1]);
  or or_1 (Y, and_1_out, and_2_out);
endmodule
