// Digital circuit JR_SEL.dig as structural Verilog
module JR_SEL (
  input  [7:0] S,
  output Y
);

  wire not_1_out;

  not not_1 (not_1_out, S[3]);
  and and_1 (Y, S[4], not_1_out, S[2], S[1], S[0]);
endmodule
