// Digital circuit KB-16.dig as structural Verilog
module KB_16 (
  input  [15:0] D,
  input  CLK,
  input  W,
  input  B_EN,
  input  A_EN,
  input  CLR,
  input  SET,
  output [15:0] B,
  output [15:0] A,
  output [15:0] Q
);

  wire CLK_t, CLR_COUNT, CLR_t;

  and and_1 (CLK_t, CLK, W);
  or or_1 (CLR_t, CLR, CLR_COUNT);
  D_FF_AS #(.Bits(16)) d_ff_as_1 (.Set(SET), .D(D), .C(CLK_t), .Clr(CLR_t), .Q(Q));  // open: nQ
  BUF_16 buf_16_1 (.A(Q), .EN1(B_EN), .EN2(B_EN), .Y(B));
  BUF_16 buf_16_2 (.A(Q), .EN1(A_EN), .EN2(A_EN), .Y(A));

  // Other names for the same wires on the sheet: CLK_RAW = CLK
endmodule
