// Digital circuit LAST_PC.dig as structural Verilog
module LAST_PC (
  input  [15:0] PC_IN,
  input  CLK,
  output [15:0] PC_OUT
);

  D_FF #(.Bits(16)) d_ff_1 (.D(PC_IN), .C(~CLK), .Q(PC_OUT));  // open: nQ
endmodule
