// Digital circuit LOAD_SEL.dig as structural Verilog
module LOAD_SEL (
  input  [7:0] S,
  input  PK,
  output Y
);

  wire and_1_out;

  and and_1 (and_1_out, S[4], ~S[3], ~S[2], ~S[1], ~S[0]);  // And
  or or_1 (Y, and_1_out, PK);

  // Notes on the sheet:
  //   PK: Enables output high
endmodule
