// Digital circuit MUL-16.dig as structural Verilog
module MUL_16 (
  input  [15:0] A,
  input  [15:0] B,
  output [15:0] CH,
  output [15:0] CL
);

  wire [7:0] _2xha_8_1_cry, _3xha_8_1_cry, _4xha_8_1_cry, mul_8_1_ch, mul_8_1_cl, mul_8_2_ch, mul_8_2_cl,
       mul_8_3_ch, mul_8_3_cl, mul_8_4_ch;

  MUL_8 mul_8_1 (.A(B[15:8]), .B(A[15:8]), .CH(mul_8_1_ch), .CL(mul_8_1_cl));
  MUL_8 mul_8_2 (.A(A[7:0]), .B(B[15:8]), .CH(mul_8_2_ch), .CL(mul_8_2_cl));
  MUL_8 mul_8_3 (.A(A[15:8]), .B(B[7:0]), .CH(mul_8_3_ch), .CL(mul_8_3_cl));
  MUL_8 mul_8_4 (.A(B[7:0]), .B(A[7:0]), .CH(mul_8_4_ch), .CL(CL[7:0]));
  _3xHA_8 _3xha_8_1 (.A(mul_8_2_cl), .B(mul_8_3_cl), .C(mul_8_4_ch), .SUM(CL[15:8]), .CRY(_3xha_8_1_cry));
  _2xHA_8 _2xha_8_1 (.A(mul_8_1_ch), .B(_4xha_8_1_cry), .SUM(CH[15:8]), .CRY(_2xha_8_1_cry));
  _4xHA_8 _4xha_8_1 (
    .A(mul_8_1_cl), .B(_3xha_8_1_cry), .C(mul_8_2_ch), .D(mul_8_3_ch), .SUM(CH[7:0]), .CRY(_4xha_8_1_cry));

  // Other names for the same wires on the sheet: AL[7:0] = A[7:0]; AH[7:0] = A[15:8]; BL[7:0] = B[7:0];
  //   BH[7:0] = B[15:8]

  // Notes on the sheet:
  //   For signed multiplication
  //   If |ANS| < 2^(16-1) then works fine
  //   If |ANS| >= 2^(16-1) then wont consistently give correct answer
  //   sometimes |ANS| >= 2^(16-1) where sign is preserved in CH
endmodule
