// Digital circuit MUL-2.dig as structural Verilog
module MUL_2 (
  input  [1:0] A,
  input  [1:0] B,
  output [1:0] CH,
  output [1:0] CL
);

  wire and_1_out, and_2_out, and_3_out, and_5_out;

  and and_1 (and_1_out, A[1], B[1]);
  and and_2 (and_2_out, B[1], A[0]);
  and and_3 (and_3_out, A[1], B[0]);
  and and_4 (CL[0], A[0], B[0]);
  and and_5 (and_5_out, and_2_out, and_3_out);
  xor xor_1 (CL[1], and_2_out, and_3_out);
  and and_6 (CH[1], and_1_out, and_5_out);
  xor xor_2 (CH[0], and_1_out, and_5_out);
endmodule
