// Digital circuit MUL-4.dig as structural Verilog
module MUL_4 (
  input  [3:0] A,
  input  [3:0] B,
  output [3:0] CH,
  output [3:0] CL
);

  wire [1:0] _2xha_2_1_cry, _3xha_2_1_cry, _4xha_2_1_cry, mul_2_1_ch, mul_2_1_cl, mul_2_2_ch, mul_2_2_cl,
       mul_2_3_ch, mul_2_3_cl, mul_2_4_ch;

  MUL_2 mul_2_1 (.A(B[3:2]), .B(A[3:2]), .CH(mul_2_1_ch), .CL(mul_2_1_cl));
  MUL_2 mul_2_2 (.A(A[1:0]), .B(B[3:2]), .CH(mul_2_2_ch), .CL(mul_2_2_cl));
  MUL_2 mul_2_3 (.A(A[3:2]), .B(B[1:0]), .CH(mul_2_3_ch), .CL(mul_2_3_cl));
  MUL_2 mul_2_4 (.A(B[1:0]), .B(A[1:0]), .CH(mul_2_4_ch), .CL(CL[1:0]));
  _2xHA_2 _2xha_2_1 (.A(mul_2_1_ch), .B(_4xha_2_1_cry), .SUM(CH[3:2]), .CRY(_2xha_2_1_cry));
  _4xHA_2 _4xha_2_1 (
    .A(mul_2_1_cl), .B(_3xha_2_1_cry), .C(mul_2_2_ch), .D(mul_2_3_ch), .SUM(CH[1:0]), .CRY(_4xha_2_1_cry));
  _3xHA_2 _3xha_2_1 (.A(mul_2_2_cl), .B(mul_2_3_cl), .C(mul_2_4_ch), .SUM(CL[3:2]), .CRY(_3xha_2_1_cry));

  // Other names for the same wires on the sheet: AL[1:0] = A[1:0]; AH[1:0] = A[3:2]; BL[1:0] = B[1:0];
  //   BH[1:0] = B[3:2]
endmodule
