// Digital circuit MUL-8.dig as structural Verilog
module MUL_8 (
  input  [7:0] A,
  input  [7:0] B,
  output [7:0] CH,
  output [7:0] CL
);

  wire [3:0] _2xha_4_1_cry, _3xha_4_1_cry, _4xha_4_1_cry, mul_4_1_ch, mul_4_1_cl, mul_4_2_ch, mul_4_2_cl,
       mul_4_3_ch, mul_4_3_cl, mul_4_4_ch;

  MUL_4 mul_4_1 (.A(B[7:4]), .B(A[7:4]), .CH(mul_4_1_ch), .CL(mul_4_1_cl));
  MUL_4 mul_4_2 (.A(A[3:0]), .B(B[7:4]), .CH(mul_4_2_ch), .CL(mul_4_2_cl));
  MUL_4 mul_4_3 (.A(A[7:4]), .B(B[3:0]), .CH(mul_4_3_ch), .CL(mul_4_3_cl));
  MUL_4 mul_4_4 (.A(B[3:0]), .B(A[3:0]), .CH(mul_4_4_ch), .CL(CL[3:0]));
  _3xHA_4 _3xha_4_1 (.A(mul_4_2_cl), .B(mul_4_3_cl), .C(mul_4_4_ch), .SUM(CL[7:4]), .CRY(_3xha_4_1_cry));
  _2xHA_4 _2xha_4_1 (.A(mul_4_1_ch), .B(_4xha_4_1_cry), .SUM(CH[7:4]), .CRY(_2xha_4_1_cry));
  _4xHA_4 _4xha_4_1 (
    .A(mul_4_1_cl), .B(_3xha_4_1_cry), .C(mul_4_2_ch), .D(mul_4_3_ch), .SUM(CH[3:0]), .CRY(_4xha_4_1_cry));

  // Other names for the same wires on the sheet: AL[3:0] = A[3:0]; AH[3:0] = A[7:4]; BL[3:0] = B[3:0];
  //   BH[3:0] = B[7:4]
endmodule
