// Digital circuit MUX-1.dig as structural Verilog
module MUX_1 (
  input  A,
  input  B,
  input  A__B,
  output Y
);

  wire and_1_out, and_2_out, not_1_out;

  and and_1 (and_1_out, A, not_1_out);
  not not_1 (not_1_out, A__B);
  and and_2 (and_2_out, B, A__B);
  or or_1 (Y, and_1_out, and_2_out);
endmodule
