// Digital circuit MUX-16.dig as structural Verilog
module MUX_16 (
  input  [15:0] A,
  input  [15:0] B,
  input  A__B,
  output [15:0] Y
);

  MUX_1 mux_1_1 (.A(A[0]), .B(B[0]), .A__B(A__B), .Y(Y[0]));
  MUX_1 mux_1_2 (.A(A[1]), .B(B[1]), .A__B(A__B), .Y(Y[1]));
  MUX_1 mux_1_3 (.A(A[2]), .B(B[2]), .A__B(A__B), .Y(Y[2]));
  MUX_1 mux_1_4 (.A(A[3]), .B(B[3]), .A__B(A__B), .Y(Y[3]));
  MUX_1 mux_1_5 (.A(A[4]), .B(B[4]), .A__B(A__B), .Y(Y[4]));
  MUX_1 mux_1_6 (.A(A[5]), .B(B[5]), .A__B(A__B), .Y(Y[5]));
  MUX_1 mux_1_7 (.A(A[6]), .B(B[6]), .A__B(A__B), .Y(Y[6]));
  MUX_1 mux_1_8 (.A(A[7]), .B(B[7]), .A__B(A__B), .Y(Y[7]));
  MUX_1 mux_1_9 (.A(A[8]), .B(B[8]), .A__B(A__B), .Y(Y[8]));
  MUX_1 mux_1_10 (.A(A[9]), .B(B[9]), .A__B(A__B), .Y(Y[9]));
  MUX_1 mux_1_11 (.A(A[10]), .B(B[10]), .A__B(A__B), .Y(Y[10]));
  MUX_1 mux_1_12 (.A(A[11]), .B(B[11]), .A__B(A__B), .Y(Y[11]));
  MUX_1 mux_1_13 (.A(A[12]), .B(B[12]), .A__B(A__B), .Y(Y[12]));
  MUX_1 mux_1_14 (.A(A[13]), .B(B[13]), .A__B(A__B), .Y(Y[13]));
  MUX_1 mux_1_15 (.A(A[14]), .B(B[14]), .A__B(A__B), .Y(Y[14]));
  MUX_1 mux_1_16 (.A(A[15]), .B(B[15]), .A__B(A__B), .Y(Y[15]));
endmodule
