// Digital circuit MUX-16x16.dig as structural Verilog
module MUX_16x16 (
  input  [15:0] I0,
  input  [15:0] I1,
  input  [15:0] I2,
  input  [15:0] I3,
  input  [15:0] I4,
  input  [15:0] I5,
  input  [15:0] I6,
  input  [15:0] I7,
  input  [15:0] I8,
  input  [15:0] I9,
  input  [15:0] I10,
  input  [15:0] I11,
  input  [15:0] I12,
  input  [15:0] I13,
  input  [15:0] I14,
  input  [15:0] I15,
  input  [3:0] S,
  output [15:0] Y
);

  wire [15:0] mux_16x4_1_y, mux_16x4_2_y, mux_16x4_3_y, mux_16x4_4_y;

  MUX_16x4 mux_16x4_1 (.I0(I0), .I1(I1), .I2(I2), .I3(I3), .S(S[1:0]), .Y(mux_16x4_1_y));
  MUX_16x4 mux_16x4_2 (.I0(I4), .I1(I5), .I2(I6), .I3(I7), .S(S[1:0]), .Y(mux_16x4_2_y));
  MUX_16x4 mux_16x4_3 (.I0(I8), .I1(I9), .I2(I10), .I3(I11), .S(S[1:0]), .Y(mux_16x4_3_y));
  MUX_16x4 mux_16x4_4 (.I0(I12), .I1(I13), .I2(I14), .I3(I15), .S(S[1:0]), .Y(mux_16x4_4_y));
  MUX_16x4 mux_16x4_5 (.I0(mux_16x4_1_y), .I1(mux_16x4_2_y), .I2(mux_16x4_3_y), .I3(mux_16x4_4_y), .S(S[3:2]), .Y(Y));
endmodule
