// Digital circuit MUX-16x4.dig as structural Verilog
module MUX_16x4 (
  input  [15:0] I0,
  input  [15:0] I1,
  input  [15:0] I2,
  input  [15:0] I3,
  input  [1:0] S,
  output [15:0] Y
);

  wire [15:0] mux_16_1_y, mux_16_2_y;

  MUX_16 mux_16_1 (.A(I0), .B(I1), .A__B(S[0]), .Y(mux_16_1_y));
  MUX_16 mux_16_2 (.A(I2), .B(I3), .A__B(S[0]), .Y(mux_16_2_y));
  MUX_16 mux_16_3 (.A(mux_16_1_y), .B(mux_16_2_y), .A__B(S[1]), .Y(Y));
endmodule
