// Digital circuit MUX-2.dig as structural Verilog
module MUX_2 (
  input  [1:0] A,
  input  [1:0] B,
  input  A__B,
  output [1:0] Y
);

  MUX_1 mux_1_1 (.A(A[0]), .B(B[0]), .A__B(A__B), .Y(Y[0]));
  MUX_1 mux_1_2 (.A(A[1]), .B(B[1]), .A__B(A__B), .Y(Y[1]));
endmodule
