// Digital circuit MUX-32.dig as structural Verilog
module MUX_32 (
  input  [31:0] A,
  input  [31:0] B,
  input  A__B,
  output [31:0] Y
);

  MUX_16 mux_16_1 (.A(A[31:16]), .B(B[31:16]), .A__B(A__B), .Y(Y[31:16]));
  MUX_16 mux_16_2 (.A(A[15:0]), .B(B[15:0]), .A__B(A__B), .Y(Y[15:0]));
endmodule
