// Digital circuit MUX-4.dig as structural Verilog
module MUX_4 (
  input  [3:0] A,
  input  [3:0] B,
  input  A__B,
  output [3:0] Y
);

  MUX_1 mux_1_1 (.A(A[0]), .B(B[0]), .A__B(A__B), .Y(Y[0]));
  MUX_1 mux_1_2 (.A(A[1]), .B(B[1]), .A__B(A__B), .Y(Y[1]));
  MUX_1 mux_1_3 (.A(A[2]), .B(B[2]), .A__B(A__B), .Y(Y[2]));
  MUX_1 mux_1_4 (.A(A[3]), .B(B[3]), .A__B(A__B), .Y(Y[3]));
endmodule
