// Digital circuit MUX-8.dig as structural Verilog
module MUX_8 (
  input  [7:0] A,
  input  [7:0] B,
  input  A__B,
  output [7:0] Y
);

  MUX_1 mux_1_1 (.A(A[0]), .B(B[0]), .A__B(A__B), .Y(Y[0]));
  MUX_1 mux_1_2 (.A(A[1]), .B(B[1]), .A__B(A__B), .Y(Y[1]));
  MUX_1 mux_1_3 (.A(A[2]), .B(B[2]), .A__B(A__B), .Y(Y[2]));
  MUX_1 mux_1_4 (.A(A[3]), .B(B[3]), .A__B(A__B), .Y(Y[3]));
  MUX_1 mux_1_5 (.A(A[4]), .B(B[4]), .A__B(A__B), .Y(Y[4]));
  MUX_1 mux_1_6 (.A(A[5]), .B(B[5]), .A__B(A__B), .Y(Y[5]));
  MUX_1 mux_1_7 (.A(A[6]), .B(B[6]), .A__B(A__B), .Y(Y[6]));
  MUX_1 mux_1_8 (.A(A[7]), .B(B[7]), .A__B(A__B), .Y(Y[7]));
endmodule
