// Digital circuit NOT'(NEG.dig as structural Verilog
module NOT__NEG (
  input  [15:0] A,
  input  PASS,
  input  NOT__NEG,
  output [15:0] Y,
  output CRY
);

  wire and_1_out;
  wire [15:0] xor_9_out;

  xor xor_1 (xor_9_out[0], A[0], PASS);
  xor xor_2 (xor_9_out[1], A[1], PASS);
  xor xor_3 (xor_9_out[2], A[2], PASS);
  xor xor_4 (xor_9_out[3], A[3], PASS);
  xor xor_5 (xor_9_out[4], A[4], PASS);
  xor xor_6 (xor_9_out[5], A[5], PASS);
  xor xor_7 (xor_9_out[6], A[6], PASS);
  xor xor_8 (xor_9_out[7], A[7], PASS);
  xor xor_9 (xor_9_out[8], A[8], PASS);
  xor xor_10 (xor_9_out[9], A[9], PASS);
  xor xor_11 (xor_9_out[10], A[10], PASS);
  xor xor_12 (xor_9_out[11], A[11], PASS);
  xor xor_13 (xor_9_out[12], A[12], PASS);
  xor xor_14 (xor_9_out[13], A[13], PASS);
  xor xor_15 (xor_9_out[14], A[14], PASS);
  xor xor_16 (xor_9_out[15], A[15], PASS);
  and and_1 (and_1_out, PASS, NOT__NEG);
  INC_16 inc_16_1 (.A(xor_9_out), .INC(and_1_out), .Y(Y), .CRY(CRY));
endmodule
