// Digital circuit OP_DEC.dig as structural Verilog
module OP_DEC (
  input  [7:0] S,
  output [3:0] OP
);

  wire and_1_out, and_2_out, and_3_out, and_4_out, and_5_out, and_6_out, and_7_out, and_8_out, or_1_out;

  and and_1 (and_1_out, ~S[4], S[3], S[2], ~S[1], S[0]);  // And
  and and_2 (and_2_out, ~S[4], S[3], S[2], ~S[1], ~S[0]);  // And
  and and_3 (and_3_out, ~S[4], S[3], ~S[2], S[1], S[0]);  // And
  and and_4 (and_4_out, S[4], ~S[3], S[2], S[1], S[0]);  // And
  and and_5 (and_5_out, S[4], ~S[3], ~S[2], S[1], ~S[0]);  // And
  and and_6 (and_6_out, S[4], ~S[3], ~S[2], S[1], S[0]);  // And
  and and_7 (and_7_out, S[4], ~S[3], S[2], ~S[1], ~S[0]);  // And
  and and_8 (and_8_out, S[4], ~S[3], S[2], S[1], ~S[0]);  // And
  or or_1 (or_1_out, and_1_out, and_2_out, and_3_out, and_4_out, and_5_out, and_6_out, and_7_out, and_8_out);
  assign OP = ~or_1_out ? S[3:0] : 4'bz;  // DriverInvSel driverinvsel_1
  assign OP = and_1_out ? 4'b0010 : 4'bz;  // Driver driver_1
  assign OP = and_2_out ? 4'b0001 : 4'bz;  // Driver driver_2
  assign OP = and_3_out ? 4'b0000 : 4'bz;  // Driver driver_3
  assign OP = and_4_out ? 4'b1010 : 4'bz;  // Driver driver_4
  assign OP = and_5_out ? 4'b1110 : 4'bz;  // Driver driver_5
  assign OP = and_6_out ? 4'b1111 : 4'bz;  // Driver driver_6
  assign OP = and_7_out ? 4'b1111 : 4'bz;  // Driver driver_7
  assign OP = and_8_out ? 4'b1010 : 4'bz;  // Driver driver_8
endmodule
