// Digital circuit PC-16.dig as structural Verilog
module PC_16 (
  input  [15:0] D,
  input  CLK,
  input  W,
  input  B_EN,
  input  A_EN,
  input  CLR,
  input  SET,
  input  INC,
  output [15:0] B,
  output [15:0] A,
  output [15:0] Q
);

  wire ha_1_1_cry, ha_1_2_cry, ha_1_3_cry, ha_1_4_cry, ha_1_5_cry, ha_1_6_cry, ha_1_7_cry, ha_1_8_cry,
       ha_1_9_cry, ha_1_10_cry, ha_1_11_cry, ha_1_12_cry, ha_1_13_cry, ha_1_14_cry, ha_1_16_cry;
  wire [15:0] ha_1_2_sum, mux_16_1_y;

  HA_1 ha_1_1 (.A(Q[1]), .B(ha_1_2_cry), .SUM(ha_1_2_sum[1]), .CRY(ha_1_1_cry));
  HA_1 ha_1_2 (.A(Q[0]), .B(INC), .SUM(ha_1_2_sum[0]), .CRY(ha_1_2_cry));
  HA_1 ha_1_3 (.A(Q[5]), .B(ha_1_4_cry), .SUM(ha_1_2_sum[5]), .CRY(ha_1_3_cry));
  HA_1 ha_1_4 (.A(Q[4]), .B(ha_1_5_cry), .SUM(ha_1_2_sum[4]), .CRY(ha_1_4_cry));
  HA_1 ha_1_5 (.A(Q[3]), .B(ha_1_6_cry), .SUM(ha_1_2_sum[3]), .CRY(ha_1_5_cry));
  HA_1 ha_1_6 (.A(Q[2]), .B(ha_1_1_cry), .SUM(ha_1_2_sum[2]), .CRY(ha_1_6_cry));
  HA_1 ha_1_7 (.A(Q[9]), .B(ha_1_8_cry), .SUM(ha_1_2_sum[9]), .CRY(ha_1_7_cry));
  HA_1 ha_1_8 (.A(Q[8]), .B(ha_1_9_cry), .SUM(ha_1_2_sum[8]), .CRY(ha_1_8_cry));
  HA_1 ha_1_9 (.A(Q[7]), .B(ha_1_10_cry), .SUM(ha_1_2_sum[7]), .CRY(ha_1_9_cry));
  HA_1 ha_1_10 (.A(Q[6]), .B(ha_1_3_cry), .SUM(ha_1_2_sum[6]), .CRY(ha_1_10_cry));
  HA_1 ha_1_11 (.A(Q[13]), .B(ha_1_12_cry), .SUM(ha_1_2_sum[13]), .CRY(ha_1_11_cry));
  HA_1 ha_1_12 (.A(Q[12]), .B(ha_1_13_cry), .SUM(ha_1_2_sum[12]), .CRY(ha_1_12_cry));
  HA_1 ha_1_13 (.A(Q[11]), .B(ha_1_14_cry), .SUM(ha_1_2_sum[11]), .CRY(ha_1_13_cry));
  HA_1 ha_1_14 (.A(Q[10]), .B(ha_1_7_cry), .SUM(ha_1_2_sum[10]), .CRY(ha_1_14_cry));
  HA_1 ha_1_15 (.A(Q[15]), .B(ha_1_16_cry), .SUM(ha_1_2_sum[15]));  // open: CRY
  HA_1 ha_1_16 (.A(Q[14]), .B(ha_1_11_cry), .SUM(ha_1_2_sum[14]), .CRY(ha_1_16_cry));
  MUX_16 mux_16_1 (.A(ha_1_2_sum), .B(D), .A__B(W), .Y(mux_16_1_y));
  D_FF_AS #(.Bits(16)) d_ff_as_1 (.Set(SET), .D(mux_16_1_y), .C(~CLK), .Clr(CLR), .Q(Q));  // open: nQ
  BUF_16 buf_16_1 (.A(Q), .EN1(B_EN), .EN2(B_EN), .Y(B));
  BUF_16 buf_16_2 (.A(Q), .EN1(A_EN), .EN2(A_EN), .Y(A));
endmodule
