// Digital circuit REG-16.dig as structural Verilog
module REG_16 (
  input  [15:0] D,
  input  CLK,
  input  W,
  input  B_EN,
  input  A_EN,
  input  CLR,
  input  SET,
  output [15:0] B,
  output [15:0] A,
  output [15:0] Q
);

  wire CLK_H, CLK_L;

  and and_1 (CLK_H, CLK, W);
  and and_2 (CLK_L, CLK, W);
  D_FF_AS #(.Bits(8)) d_ff_as_1 (.Set(SET), .D(D[15:8]), .C(CLK_H), .Clr(CLR), .Q(Q[15:8]));  // open: nQ
  D_FF_AS #(.Bits(8)) d_ff_as_2 (.Set(SET), .D(D[7:0]), .C(CLK_L), .Clr(CLR), .Q(Q[7:0]));  // open: nQ
  BUF_16 buf_16_1 (.A(Q), .EN1(B_EN), .EN2(B_EN), .Y(B));
  BUF_16 buf_16_2 (.A(Q), .EN1(A_EN), .EN2(A_EN), .Y(A));
endmodule
