// Digital circuit REGZERO-16.dig as structural Verilog
module REGZERO_16 (
  input  EN,
  input  B_EN,
  input  A_EN,
  output [15:0] B,
  output [15:0] A
);

  wire and_1_out, and_2_out;

  and and_1 (and_1_out, EN, B_EN);
  and and_2 (and_2_out, EN, A_EN);
  assign B = and_1_out ? {16{1'b0}} : 16'bz;  // Driver driver_1
  assign A = and_2_out ? {16{1'b0}} : 16'bz;  // Driver driver_2
endmodule
