// Digital circuit SGT-1.dig as structural Verilog
module SGT_1 (
  input  A,
  input  B,
  output GT,
  output EQ
);

  wire not_1_out;

  not not_1 (not_1_out, B);
  xnor xnor_1 (EQ, A, B);
  and and_1 (GT, A, not_1_out);
endmodule
