// Digital circuit SLT-1.dig as structural Verilog
module SLT_1 (
  input  A,
  input  B,
  output LT,
  output EQ
);

  wire not_1_out;

  not not_1 (not_1_out, A);
  and and_1 (LT, not_1_out, B);
  xnor xnor_1 (EQ, A, B);

  // Notes on the sheet:
  //   A < B
endmodule
