// Digital circuit SLT-16.dig as structural Verilog
module SLT_16 (
  input  [15:0] A,
  input  [15:0] B,
  output [15:0] LT,
  output [15:0] EQ
);

  wire and_2_out, and_3_out, and_4_out, and_5_out, and_6_out, and_7_out, and_8_out, and_9_out, and_10_out,
       and_11_out, and_12_out, and_13_out, and_14_out, and_15_out, and_16_out, slt_1_1_eq, slt_1_1_lt,
       slt_1_2_eq, slt_1_2_lt, slt_1_3_eq, slt_1_3_lt, slt_1_4_eq, slt_1_4_lt, slt_1_5_eq, slt_1_5_lt,
       slt_1_6_eq, slt_1_6_lt, slt_1_7_eq, slt_1_7_lt, slt_1_8_eq, slt_1_8_lt, slt_1_9_eq, slt_1_9_lt,
       slt_1_10_eq, slt_1_10_lt, slt_1_11_eq, slt_1_11_lt, slt_1_12_eq, slt_1_12_lt, slt_1_13_eq,
       slt_1_13_lt, slt_1_14_eq, slt_1_14_lt, slt_1_15_eq, slt_1_15_lt, slt_1_16_eq, slt_1_16_lt;

  SLT_1 slt_1_1 (.A(A[15]), .B(B[15]), .LT(slt_1_1_lt), .EQ(slt_1_1_eq));
  SLT_1 slt_1_2 (.A(A[14]), .B(B[14]), .LT(slt_1_2_lt), .EQ(slt_1_2_eq));
  SLT_1 slt_1_3 (.A(A[13]), .B(B[13]), .LT(slt_1_3_lt), .EQ(slt_1_3_eq));
  SLT_1 slt_1_4 (.A(A[12]), .B(B[12]), .LT(slt_1_4_lt), .EQ(slt_1_4_eq));
  SLT_1 slt_1_5 (.A(A[11]), .B(B[11]), .LT(slt_1_5_lt), .EQ(slt_1_5_eq));
  SLT_1 slt_1_6 (.A(A[10]), .B(B[10]), .LT(slt_1_6_lt), .EQ(slt_1_6_eq));
  SLT_1 slt_1_7 (.A(A[9]), .B(B[9]), .LT(slt_1_7_lt), .EQ(slt_1_7_eq));
  SLT_1 slt_1_8 (.A(A[8]), .B(B[8]), .LT(slt_1_8_lt), .EQ(slt_1_8_eq));
  SLT_1 slt_1_9 (.A(A[7]), .B(B[7]), .LT(slt_1_9_lt), .EQ(slt_1_9_eq));
  SLT_1 slt_1_10 (.A(A[6]), .B(B[6]), .LT(slt_1_10_lt), .EQ(slt_1_10_eq));
  SLT_1 slt_1_11 (.A(A[5]), .B(B[5]), .LT(slt_1_11_lt), .EQ(slt_1_11_eq));
  SLT_1 slt_1_12 (.A(A[4]), .B(B[4]), .LT(slt_1_12_lt), .EQ(slt_1_12_eq));
  SLT_1 slt_1_13 (.A(A[3]), .B(B[3]), .LT(slt_1_13_lt), .EQ(slt_1_13_eq));
  SLT_1 slt_1_14 (.A(A[2]), .B(B[2]), .LT(slt_1_14_lt), .EQ(slt_1_14_eq));
  SLT_1 slt_1_15 (.A(A[1]), .B(B[1]), .LT(slt_1_15_lt), .EQ(slt_1_15_eq));
  SLT_1 slt_1_16 (.A(A[0]), .B(B[0]), .LT(slt_1_16_lt), .EQ(slt_1_16_eq));
  and and_1 (EQ[0], slt_1_1_eq, slt_1_2_eq, slt_1_3_eq, slt_1_4_eq, slt_1_5_eq, slt_1_6_eq, slt_1_7_eq, slt_1_8_eq, slt_1_9_eq, slt_1_10_eq, slt_1_11_eq, slt_1_12_eq, slt_1_13_eq, slt_1_14_eq, slt_1_15_eq, slt_1_16_eq);
  and and_2 (and_2_out, slt_1_1_eq, slt_1_2_lt);
  and and_3 (and_3_out, slt_1_1_eq, slt_1_2_eq, slt_1_3_lt);
  and and_4 (and_4_out, slt_1_1_eq, slt_1_2_eq, slt_1_3_eq, slt_1_4_lt);
  and and_5 (and_5_out, slt_1_1_eq, slt_1_2_eq, slt_1_3_eq, slt_1_4_eq, slt_1_5_lt);
  and and_6 (and_6_out, slt_1_1_eq, slt_1_2_eq, slt_1_3_eq, slt_1_4_eq, slt_1_5_eq, slt_1_6_lt);
  and and_7 (and_7_out, slt_1_1_eq, slt_1_2_eq, slt_1_3_eq, slt_1_4_eq, slt_1_5_eq, slt_1_6_eq, slt_1_7_lt);
  and and_8 (and_8_out, slt_1_1_eq, slt_1_2_eq, slt_1_3_eq, slt_1_4_eq, slt_1_5_eq, slt_1_6_eq, slt_1_7_eq, slt_1_8_lt);
  and and_9 (and_9_out, slt_1_1_eq, slt_1_2_eq, slt_1_3_eq, slt_1_4_eq, slt_1_5_eq, slt_1_6_eq, slt_1_7_eq, slt_1_8_eq, slt_1_9_lt);
  and and_10 (and_10_out, slt_1_1_eq, slt_1_2_eq, slt_1_3_eq, slt_1_4_eq, slt_1_5_eq, slt_1_6_eq, slt_1_7_eq, slt_1_8_eq, slt_1_9_eq, slt_1_10_lt);
  and and_11 (and_11_out, slt_1_1_eq, slt_1_2_eq, slt_1_3_eq, slt_1_4_eq, slt_1_5_eq, slt_1_6_eq, slt_1_7_eq, slt_1_8_eq, slt_1_9_eq, slt_1_10_eq, slt_1_11_lt);
  and and_12 (and_12_out, slt_1_1_eq, slt_1_2_eq, slt_1_3_eq, slt_1_4_eq, slt_1_5_eq, slt_1_6_eq, slt_1_7_eq, slt_1_8_eq, slt_1_9_eq, slt_1_10_eq, slt_1_11_eq, slt_1_12_lt);
  and and_13 (and_13_out, slt_1_1_eq, slt_1_2_eq, slt_1_3_eq, slt_1_4_eq, slt_1_5_eq, slt_1_6_eq, slt_1_7_eq, slt_1_8_eq, slt_1_9_eq, slt_1_10_eq, slt_1_11_eq, slt_1_12_eq, slt_1_13_lt);
  and and_14 (and_14_out, slt_1_1_eq, slt_1_2_eq, slt_1_3_eq, slt_1_4_eq, slt_1_5_eq, slt_1_6_eq, slt_1_7_eq, slt_1_8_eq, slt_1_9_eq, slt_1_10_eq, slt_1_11_eq, slt_1_12_eq, slt_1_13_eq, slt_1_14_lt);
  and and_15 (and_15_out, slt_1_1_eq, slt_1_2_eq, slt_1_3_eq, slt_1_4_eq, slt_1_5_eq, slt_1_6_eq, slt_1_7_eq, slt_1_8_eq, slt_1_9_eq, slt_1_10_eq, slt_1_11_eq, slt_1_12_eq, slt_1_13_eq, slt_1_14_eq, slt_1_15_lt);
  and and_16 (and_16_out, slt_1_1_eq, slt_1_2_eq, slt_1_3_eq, slt_1_4_eq, slt_1_5_eq, slt_1_6_eq, slt_1_7_eq, slt_1_8_eq, slt_1_9_eq, slt_1_10_eq, slt_1_11_eq, slt_1_12_eq, slt_1_13_eq, slt_1_14_eq, slt_1_15_eq, slt_1_16_lt);
  or or_1 (LT[0], slt_1_1_lt, and_2_out, and_3_out, and_4_out, and_5_out, and_6_out, and_7_out, and_8_out, and_9_out, and_10_out, and_11_out, and_12_out, and_13_out, and_14_out, and_15_out, and_16_out);

  assign EQ[15:1] = {15{1'b0}};
  assign LT[15:1] = {15{1'b0}};

  // Notes on the sheet:
  //   A < B
  //   This implementation uses LT15 + EQ15*LT14 + EQ15*EQ14*LT13 --> EQ15..EQ1*LT0
  //   The gate count can be reduced with the equation LT15 + EQ15*(LT14 + EQ14*( LT13 + EQ13( --> LT1 + EQ1*(LT0))))
  //   This second equation will cut the and gates(if only 2 input ones were used which is not the case) in half. However this also creates
  //   a +16 gate long chain of AND and OR gates, which I belive would create a large propigation delay, which is why I chose the first equation,
  //   and totally not because I didnt realize the equation could be simplified after the circuit was already built.
endmodule
