// Digital circuit SYS_CLK.dig as structural Verilog
module SYS_CLK (
  input  [15:0] D,
  input  CLK,
  input  W,
  input  B_EN,
  input  A_EN,
  input  CLR,
  input  SET,
  output [15:0] B,
  output [15:0] A,
  output [15:0] Q
);

  wire and_1_out, or_1_out;

  or or_1 (or_1_out, CLR, 1'b0);
  COUNTAS_16 countas_16_1 (.D(D), .CLK(CLK), .W(W), .CLR(or_1_out), .SET(SET), .Y(Q));
  BUF_16 buf_16_1 (.A(Q), .EN1(B_EN), .EN2(B_EN), .Y(B));
  BUF_16 buf_16_2 (.A(Q), .EN1(A_EN), .EN2(A_EN), .Y(A));
  and and_1 (and_1_out, Q[7], Q[6], Q[5], Q[4], Q[3], Q[2], Q[1], Q[0]);

  // Notes on the sheet:
  //   W: if w is toggle without writing causes undefined behavior
endmodule
