// Digital circuit TEMP.dig as structural Verilog
module TEMP (
  input  in_2,
  input  in_3,
  input  in_4,
  input  [15:0] in_22,
  input  in_23,
  input  in_29,
  input  [7:0] in_32,
  input  INSTR_TEST,
  input  [23:0] in_34,
  input  [15:0] ADDR_PEAK,
  input  PEEK,
  output [15:0] out_1,
  output [15:0] out_5,
  output [15:0] out_6,
  output [15:0] out_7,
  output [15:0] out_8,
  output [15:0] PC,
  output [15:0] out_10,
  output [15:0] out_11,
  output [15:0] out_12,
  output [15:0] out_13,
  output [15:0] out_14,
  output [15:0] out_15,
  output [15:0] out_16,
  output [15:0] out_17,
  output [15:0] out_18,
  output [15:0] out_19,
  output [15:0] out_20,
  output [15:0] out_21,
  output [31:0] out_24,
  output [15:0] out_25,
  output [15:0] out_26,
  output [15:0] out_27,
  output [3:0] out_28,
  output [15:0] out_30,
  output [15:0] ADDR,
  output [31:0] out_35,
  output [15:0] Q,
  output [31:0] out_39
);

  wire and_1_out, and_2_out, BNE, BRANCH, JAL, jmp_im_sel_1_y, jmp_sel_1_y, JR, LOAD, load_sel_1_y, MOV,
       mux_1_1_y, or_1_out, or_2_out, READ_A, READ_B, STORE, store_sel_2_y, WRITE_PC, WRITE_W;
  wire [3:0] mux_4_1_y, mux_4_2_y, mux_4_3_y, mux_4_4_y, mux_4_5_y, mux_4_6_y, mux_4_7_y;
  wire [15:0] A_EN, B_EN, fa_16_1_sum, inc_16_1_y, mux_16_2_y, mux_16_3_y, mux_16_4_y, mux_16_5_y, not_1_out,
       PC_IN, W;

  MUX_16 mux_16_1 (.A(PC), .B(out_25), .A__B(in_23), .Y(out_27));
  EEPROMDualPort #(.AddrBits(16), .Bits(32)) eepromdualport_1 (
    .A(out_27), .Din({32{1'b0}}), .str(1'b0), .C(in_29), .ld(1'b1), .D(out_35));
  MUX_32 mux_32_1 (.A(out_35), .B({in_32, in_34}), .A__B(INSTR_TEST), .Y(out_24));
  OP_DEC op_dec_1 (.S(out_24[31:24]), .OP(out_28));
  W_SEL w_sel_1 (.S(out_24[31:24]), .Y(WRITE_W));
  B_SEL b_sel_1 (.S(out_24[31:24]), .Y(READ_B));
  A_SEL a_sel_1 (.S(out_24[31:24]), .Y(READ_A));
  STORE_SEL store_sel_1 (.S(out_24[31:24]), .Y(STORE));
  BRANCH_SEL branch_sel_1 (.S(out_24[31:24]), .Y(BRANCH));
  BNE_SEL bne_sel_1 (.S(out_24[31:24]), .Y(BNE));
  JR_SEL jr_sel_1 (.S(out_24[31:24]), .Y(JR));
  JAL_SEL jal_sel_1 (.S(out_24[31:24]), .Y(JAL));
  MOV_SEL mov_sel_1 (.S(out_24[31:24]), .Y(MOV));
  MUX_16 mux_16_2 (.A(out_24[15:0]), .B(out_24[19:4]), .A__B(MOV), .Y(mux_16_2_y));
  MUX_16 mux_16_3 (.A(mux_16_2_y), .B(out_26), .A__B(READ_A), .Y(mux_16_3_y));
  and and_1 (and_1_out, WRITE_W, ~WRITE_PC, ~BRANCH);  // And
  assign not_1_out = ~out_30;  // Not not_1, 16 bits wide
  INC_16 inc_16_1 (.A(mux_16_3_y), .INC(JAL), .Y(inc_16_1_y));  // open: CRY
  MUX_4 mux_4_1 (.A(4'b0000), .B(out_24[19:16]), .A__B(READ_B), .Y(mux_4_1_y));
  MUX_4 mux_4_2 (.A(4'b0000), .B(out_24[15:12]), .A__B(READ_A), .Y(mux_4_2_y));
  or or_1 (or_1_out, BRANCH, STORE);
  MUX_1 mux_1_1 (.A(out_30[0]), .B(not_1_out[0]), .A__B(BNE), .Y(mux_1_1_y));
  MUX_16 mux_16_4 (.A(in_22), .B(out_25), .A__B(READ_B), .Y(mux_16_4_y));
  MUX_4 mux_4_3 (.A(4'b0000), .B(out_24[23:20]), .A__B(and_1_out), .Y(mux_4_3_y));
  or or_2 (or_2_out, BRANCH, JR, STORE);
  JMP_IM_SEL jmp_im_sel_1 (.S(out_24[31:24]), .Y(jmp_im_sel_1_y));
  JMP_SEL jmp_sel_1 (.S(out_24[31:24]), .Y(jmp_sel_1_y));
  and and_2 (and_2_out, mux_1_1_y, BRANCH);
  MUX_4 mux_4_4 (.A(mux_4_1_y), .B(out_24[23:20]), .A__B(or_2_out), .Y(mux_4_4_y));
  MUX_4 mux_4_5 (.A(mux_4_2_y), .B(out_24[19:16]), .A__B(or_1_out), .Y(mux_4_5_y));
  MUX_16 mux_16_5 (.A(out_25), .B(out_24[23:8]), .A__B(jmp_im_sel_1_y), .Y(mux_16_5_y));
  or or_3 (WRITE_PC, jmp_sel_1_y, and_2_out);
  ALU alu_1 (.B(mux_16_4_y), .A(inc_16_1_y), .CLR(in_3), .CLK(in_2), .CIN(in_4), .S(out_28), .YH(out_6), .YL(out_5));
  MUX_4 mux_4_6 (.A(mux_4_3_y), .B(out_24[7:4]), .A__B(JAL), .Y(mux_4_6_y));
  MUX_4 mux_4_7 (.A(mux_4_5_y), .B(4'b0011), .A__B(JAL), .Y(mux_4_7_y));
  assign out_30 = ~LOAD ? out_5 : 16'bz;  // DriverInvSel driverinvsel_1
  // DEC_4C dec_4c_1: pin names not known; wires that end beside it: mux_4_6_y, 1'b1, W
  // DEC_4C dec_4c_2: pin names not known; wires that end beside it: mux_4_4_y, 1'b1, B_EN
  // DEC_4C dec_4c_3: pin names not known; wires that end beside it: mux_4_7_y, 1'b1, A_EN
  MUX_16 mux_16_6 (.A(mux_16_5_y), .B(out_24[15:0]), .A__B(BRANCH), .Y(PC_IN));
  ZER0_16 zer0_16_1 (.B(out_25), .A(out_26), .Q(out_1), .EN(1'b1), .B_EN(B_EN[0]), .A_EN(A_EN[0]));
  REG_16 reg_16_1 (
    .D(out_30), .CLK(in_29), .W(W[1]), .B_EN(B_EN[1]), .A_EN(A_EN[1]), .CLR(1'b0), .SET(1'b0), .B(out_25),
    .A(out_26), .Q(out_8));
  REG_16 reg_16_2 (
    .D(out_30), .CLK(in_29), .W(W[2]), .B_EN(B_EN[2]), .A_EN(A_EN[2]), .CLR(1'b0), .SET(1'b0), .B(out_25),
    .A(out_26), .Q(out_7));
  PC_16 pc_16_1 (
    .D(PC_IN), .CLK(in_29), .W(WRITE_PC), .B_EN(B_EN[3]), .A_EN(A_EN[3]), .CLR(1'b0), .SET(1'b0), .INC(1'b1),
    .B(out_25), .A(out_26), .Q(PC));
  REG_16 reg_16_3 (
    .D(out_30), .CLK(in_29), .W(W[4]), .B_EN(B_EN[4]), .A_EN(A_EN[4]), .CLR(1'b0), .SET(1'b0), .B(out_25),
    .A(out_26), .Q(out_13));
  REG_16 reg_16_4 (
    .D(out_30), .CLK(in_29), .W(W[5]), .B_EN(B_EN[5]), .A_EN(A_EN[5]), .CLR(1'b0), .SET(1'b0), .B(out_25),
    .A(out_26), .Q(out_10));
  REG_16 reg_16_5 (
    .D(out_30), .CLK(in_29), .W(W[6]), .B_EN(B_EN[6]), .A_EN(A_EN[6]), .CLR(1'b0), .SET(1'b0), .B(out_25),
    .A(out_26), .Q(out_11));
  REG_16 reg_16_6 (
    .D(out_30), .CLK(in_29), .W(W[7]), .B_EN(B_EN[7]), .A_EN(A_EN[7]), .CLR(1'b0), .SET(1'b0), .B(out_25),
    .A(out_26), .Q(out_12));
  STORE_SEL store_sel_2 (.S(out_24[31:24]), .Y(store_sel_2_y));
  LOAD_SEL load_sel_1 (.S(out_24[31:24]), .Y(load_sel_1_y));
  REG_16 reg_16_7 (
    .D(out_30), .CLK(in_29), .W(W[8]), .B_EN(B_EN[8]), .A_EN(A_EN[8]), .CLR(1'b0), .SET(1'b0), .B(out_25),
    .A(out_26), .Q(out_17));
  REG_16 reg_16_8 (
    .D(out_30), .CLK(in_29), .W(W[9]), .B_EN(B_EN[9]), .A_EN(A_EN[9]), .CLR(1'b0), .SET(1'b0), .B(out_25),
    .A(out_26), .Q(out_14));
  REG_16 reg_16_9 (
    .D(out_30), .CLK(in_29), .W(W[10]), .B_EN(B_EN[10]), .A_EN(A_EN[10]), .CLR(1'b0), .SET(1'b0), .B(out_25),
    .A(out_26), .Q(out_15));
  REG_16 reg_16_10 (
    .D(out_30), .CLK(in_29), .W(W[11]), .B_EN(B_EN[11]), .A_EN(A_EN[11]), .CLR(1'b0), .SET(1'b0), .B(out_25),
    .A(out_26), .Q(out_16));
  FA_16 fa_16_1 (.A(out_24[15:0]), .B(out_25), .CIN(1'b0), .SUM(fa_16_1_sum));  // open: CRY
  MUX_16 mux_16_7 (.A(fa_16_1_sum), .B(ADDR_PEAK), .A__B(PEEK), .Y(ADDR));
  or or_4 (LOAD, PEEK, load_sel_1_y);
  RAMDualPort #(.AddrBits(16), .Bits(16)) ramdualport_1 (
    .A(ADDR), .Din(out_26), .str(store_sel_2_y), .C(in_29), .ld(LOAD), .D(out_30));
  REG_16 reg_16_11 (
    .D(out_30), .CLK(in_29), .W(W[12]), .B_EN(B_EN[12]), .A_EN(A_EN[12]), .CLR(1'b0), .SET(1'b0), .B(out_25),
    .A(out_26), .Q(out_21));
  REG_16 reg_16_12 (
    .D(out_30), .CLK(in_29), .W(W[13]), .B_EN(B_EN[13]), .A_EN(A_EN[13]), .CLR(1'b0), .SET(1'b0), .B(out_25),
    .A(out_26), .Q(out_18));
  REG_16 reg_16_13 (
    .D(out_30), .CLK(in_29), .W(W[14]), .B_EN(B_EN[14]), .A_EN(A_EN[14]), .CLR(1'b0), .SET(1'b0), .B(out_25),
    .A(out_26), .Q(out_19));
  REG_16 reg_16_14 (
    .D(out_30), .CLK(in_29), .W(W[15]), .B_EN(B_EN[15]), .A_EN(A_EN[15]), .CLR(1'b0), .SET(1'b0), .B(out_25),
    .A(out_26), .Q(out_20));

  assign out_39 = out_24;
  assign Q = out_30;

  // Other names for the same wires on the sheet: A_OUT[15:0] = out_26; B_OUT[15:0] = out_25; CLK = in_29;
  //   CLK_16[15:0] = {16{in_29}}; _0_15[15:0] = out_24[15:0]; INSTR[31:0] = out_24; _4_7[3:0] = out_24[7:4];
  //   _4_19[15:0] = out_24[19:4]; _8_23[15:0] = out_24[23:8]; _12_15[3:0] = out_24[15:12];
  //   _16_19[3:0] = out_24[19:16]; _20_23[3:0] = out_24[23:20]; _24_31[7:0] = out_24[31:24]; OP[3:0] = out_28;
  //   USE_PC = in_23; YH[15:0] = out_6; YL[15:0] = out_30

  // Notes on the sheet:
  //   contents of eepromdualport_1 (hex, n*v repeats v):
  //   1a500020,1a600050,1a700080,15002f00,2fee000,17200000,14850008
  //   ,f80000,17200000,bff0001,bee0001,15003a00,867000,1976000,2a75000
  //   ,3b55000,11080000,11090001,110a0002,110b0003,10b00000,10a00001
  //   ,10900002,10800003,15003a00,4875000,5955000,1aa00070,6aa6000,7b65000
  //   ,8c65000,9d60000,15003a00,b800001,c900001,da70000,eb56000,ec65000
  //   ,fd56000,fe66000,15003a00,1a800000,1a900050,16000620,b880001,1289002b
  //   ,15003a00,1a800020,1a900020,1aa00020,1ab00000,14890009,cf00001
  //   ,148a0009,ce00001,148b0009,cd00001,15003a00
  //   ZERO
  //   SP
  //   LR
  //   HI
  //   R0
  //   R1
  //   R2
  //   R3
  //   R4
  //   R5
  //   R6
  //   R7
endmodule
