// Digital circuit W DEC.dig as structural Verilog
module W_DEC (
  input  [3:0] OP,
  input  [3:0] REG,
  output [3:0] Y
);

  wire and_1_out, and_2_out, and_3_out, not_1_out, not_2_out, not_3_out, not_4_out, or_1_out;

  not not_1 (not_1_out, OP[3]);
  not not_2 (not_2_out, OP[2]);
  not not_3 (not_3_out, OP[1]);
  not not_4 (not_4_out, OP[0]);
  and and_1 (and_1_out, not_1_out, OP[1]);
  and and_2 (and_2_out, OP[3], not_3_out);
  and and_3 (and_3_out, not_3_out, not_4_out);
  or or_1 (or_1_out, and_1_out, and_2_out, not_2_out, and_3_out);
  assign Y = or_1_out ? REG : 4'bz;  // Driver driver_1

  // Notes on the sheet:
  //   writie decoder, for deterimines how/if  the
  //   microprocessor will write the output
endmodule
