// Digital circuit WWSLTF-16.dig as structural Verilog
module WWSLTF_16 (
  input  [15:0] in_2,
  input  [15:0] in_3,
  output Y
);

  wire and_1_out, and_2_out, and_3_out, and_4_out, and_5_out, and_6_out, and_7_out, and_8_out, and_9_out,
       and_10_out, and_11_out, and_12_out, and_13_out, and_14_out, and_15_out, not_1_out, not_2_out,
       not_3_out, not_4_out, not_5_out, not_6_out, not_7_out, not_8_out, not_9_out, not_10_out, not_11_out,
       not_12_out, not_13_out, not_14_out, not_15_out, slt_1_1_p3, slt_1_2_p3, slt_1_3_p3, slt_1_4_p3,
       slt_1_5_p3, slt_1_6_p3, slt_1_7_p3, slt_1_8_p3, slt_1_9_p3, slt_1_10_p3, slt_1_11_p3, slt_1_12_p3,
       slt_1_13_p3, slt_1_14_p3, slt_1_15_p3, slt_1_16_p3;

  // SLT_1 slt_1_1: pin names not known; wires that end beside it: in_2[15], in_3[15], slt_1_1_p3
  // SLT_1 slt_1_2: pin names not known; wires that end beside it: in_2[14], in_3[14], slt_1_2_p3
  // SLT_1 slt_1_3: pin names not known; wires that end beside it: in_2[13], in_3[13], slt_1_3_p3
  // SLT_1 slt_1_4: pin names not known; wires that end beside it: in_2[12], in_3[12], slt_1_4_p3
  // SLT_1 slt_1_5: pin names not known; wires that end beside it: in_2[11], in_3[11], slt_1_5_p3
  // SLT_1 slt_1_6: pin names not known; wires that end beside it: in_2[10], in_3[10], slt_1_6_p3
  // SLT_1 slt_1_7: pin names not known; wires that end beside it: in_2[9], in_3[9], slt_1_7_p3
  // SLT_1 slt_1_8: pin names not known; wires that end beside it: in_2[8], in_3[8], slt_1_8_p3
  // SLT_1 slt_1_9: pin names not known; wires that end beside it: in_2[7], in_3[7], slt_1_9_p3
  // SLT_1 slt_1_10: pin names not known; wires that end beside it: in_2[6], in_3[6], slt_1_10_p3
  // SLT_1 slt_1_11: pin names not known; wires that end beside it: in_2[5], in_3[5], slt_1_11_p3
  // SLT_1 slt_1_12: pin names not known; wires that end beside it: in_2[4], in_3[4], slt_1_12_p3
  // SLT_1 slt_1_13: pin names not known; wires that end beside it: in_2[3], in_3[3], slt_1_13_p3
  // SLT_1 slt_1_14: pin names not known; wires that end beside it: in_2[2], in_3[2], slt_1_14_p3
  // SLT_1 slt_1_15: pin names not known; wires that end beside it: in_2[1], in_3[1], slt_1_15_p3
  // SLT_1 slt_1_16: pin names not known; wires that end beside it: in_2[0], in_3[0], slt_1_16_p3
  not not_1 (not_1_out, slt_1_1_p3);
  not not_2 (not_2_out, slt_1_2_p3);
  not not_3 (not_3_out, slt_1_3_p3);
  not not_4 (not_4_out, slt_1_4_p3);
  not not_5 (not_5_out, slt_1_5_p3);
  not not_6 (not_6_out, slt_1_6_p3);
  not not_7 (not_7_out, slt_1_7_p3);
  not not_8 (not_8_out, slt_1_8_p3);
  not not_9 (not_9_out, slt_1_9_p3);
  not not_10 (not_10_out, slt_1_10_p3);
  not not_11 (not_11_out, slt_1_11_p3);
  not not_12 (not_12_out, slt_1_12_p3);
  not not_13 (not_13_out, slt_1_13_p3);
  not not_14 (not_14_out, slt_1_14_p3);
  not not_15 (not_15_out, slt_1_15_p3);
  and and_1 (and_1_out, not_1_out, slt_1_2_p3);
  and and_2 (and_2_out, not_1_out, not_2_out, slt_1_3_p3);
  and and_3 (and_3_out, not_1_out, not_2_out, not_3_out, slt_1_4_p3);
  and and_4 (and_4_out, not_1_out, not_2_out, not_3_out, not_4_out, slt_1_5_p3);
  and and_5 (and_5_out, not_1_out, not_2_out, not_3_out, not_4_out, not_5_out, slt_1_6_p3);
  and and_6 (and_6_out, not_1_out, not_2_out, not_3_out, not_4_out, not_5_out, not_6_out, slt_1_7_p3);
  and and_7 (and_7_out, not_1_out, not_2_out, not_3_out, not_4_out, not_5_out, not_6_out, not_7_out, slt_1_8_p3);
  and and_8 (and_8_out, not_1_out, not_2_out, not_3_out, not_4_out, not_5_out, not_6_out, not_7_out, not_8_out, slt_1_9_p3);
  and and_9 (and_9_out, not_1_out, not_2_out, not_3_out, not_4_out, not_5_out, not_6_out, not_7_out, not_8_out, not_9_out, slt_1_10_p3);
  and and_10 (and_10_out, not_1_out, not_2_out, not_3_out, not_4_out, not_5_out, not_6_out, not_7_out, not_8_out, not_9_out, not_10_out, slt_1_11_p3);
  and and_11 (and_11_out, not_1_out, not_2_out, not_3_out, not_4_out, not_5_out, not_6_out, not_7_out, not_8_out, not_9_out, not_10_out, not_11_out, slt_1_12_p3);
  and and_12 (and_12_out, not_1_out, not_2_out, not_3_out, not_4_out, not_5_out, not_6_out, not_7_out, not_8_out, not_9_out, not_10_out, not_11_out, not_12_out, slt_1_13_p3);
  and and_13 (and_13_out, not_1_out, not_2_out, not_3_out, not_4_out, not_5_out, not_6_out, not_7_out, not_8_out, not_9_out, not_10_out, not_11_out, not_12_out, not_13_out, slt_1_14_p3);
  and and_14 (and_14_out, not_1_out, not_2_out, not_3_out, not_4_out, not_5_out, not_6_out, not_7_out, not_8_out, not_9_out, not_10_out, not_11_out, not_12_out, not_13_out, not_14_out, slt_1_15_p3);
  and and_15 (and_15_out, not_1_out, not_2_out, not_3_out, not_4_out, not_5_out, not_6_out, not_7_out, not_8_out, not_9_out, not_10_out, not_11_out, not_12_out, not_13_out, not_14_out, not_15_out, slt_1_16_p3);
  or or_1 (Y, slt_1_1_p3, and_1_out, and_2_out, and_3_out, and_4_out, and_5_out, and_6_out, and_7_out, and_8_out, and_9_out, and_10_out, and_11_out, and_12_out, and_13_out, and_14_out, and_15_out);
endmodule
